// Logisim project MultiAccessRegFile.circ as structural Verilog: 2 circuits, main circuit main
module main (
  input  [2:0] Address,
  input  [2:0] Address_2,
  input  [2:0] Address_3,
  input  [2:0] Address_4,
  input  R_W,
  input  [7:0] Data_In,
  input  R_W_2,
  input  [7:0] Data_In_2,
  input  R_W_3,
  input  [7:0] Data_In_3,
  input  R_W_4,
  input  [7:0] Data_In_4,
  input  in_13,
  output [7:0] Data_Out,
  output [7:0] Data_Out_2,
  output [7:0] Data_Out_3,
  output [7:0] Data_Out_4
);

  wire and_2_out, and_4_out, and_6_out, and_8_out, and_10_out, and_12_out, and_14_out, and_16_out,
       and_18_out, and_20_out, and_22_out, and_24_out, and_26_out, and_28_out, and_30_out, and_32_out,
       clock_1_out, comparator_1_eq, comparator_2_eq, comparator_3_eq, comparator_4_eq, comparator_5_eq,
       comparator_6_eq, comparator_7_eq, comparator_8_eq, comparator_9_eq, comparator_10_eq,
       comparator_11_eq, comparator_12_eq, comparator_13_eq, comparator_14_eq, comparator_15_eq,
       comparator_16_eq, or_1_out, or_2_out, or_3_out, or_4_out, or_5_out, or_6_out, or_7_out, or_8_out,
       or_9_out, or_10_out, or_11_out, or_12_out;
  wire [2:0] adder_1_out, adder_2_out, adder_3_out;
  wire [7:0] and_1_out, and_3_out, and_5_out, and_7_out, and_9_out, and_11_out, and_13_out, and_15_out,
       and_17_out, and_19_out, and_21_out, and_23_out, and_25_out, and_27_out, and_29_out, and_31_out,
       bit_extender_1_out, bit_extender_2_out, bit_extender_3_out, bit_extender_4_out, bit_extender_5_out,
       bit_extender_6_out, bit_extender_7_out, bit_extender_8_out, bit_extender_9_out, bit_extender_10_out,
       bit_extender_11_out, bit_extender_12_out, bit_extender_13_out, bit_extender_14_out,
       bit_extender_15_out, bit_extender_16_out, or_13_out, or_14_out, or_15_out, or_16_out, register_1_q,
       register_2_q, register_3_q, register_4_q;

  Adder #(.width(3)) adder_1 (.a(3'b000), .b(3'b001), .out(adder_1_out));  // open: cin, cout
  Adder #(.width(3)) adder_2 (.a(adder_1_out), .b(3'b001), .out(adder_2_out));  // open: cin, cout
  Adder #(.width(3)) adder_3 (.a(adder_2_out), .b(3'b001), .out(adder_3_out));  // open: cin, cout
  assign and_1_out = Data_In & bit_extender_1_out;  // AND_Gate and_1, 8 bits wide
  and and_2 (and_2_out, R_W, comparator_1_eq);
  Comparator #(.width(3), .mode("unsigned")) comparator_1 (
    .a(Address), .b(3'b000), .eq(comparator_1_eq));  // open: gt, lt
  assign bit_extender_1_out = {{7{comparator_1_eq}}, comparator_1_eq};  // Bit_Extender bit_extender_1
  assign and_3_out = Data_In & bit_extender_2_out;  // AND_Gate and_3, 8 bits wide
  and and_4 (and_4_out, R_W, comparator_2_eq);
  Comparator #(.width(3), .mode("unsigned")) comparator_2 (
    .a(Address), .b(adder_1_out), .eq(comparator_2_eq));  // open: gt, lt
  assign bit_extender_2_out = {{7{comparator_2_eq}}, comparator_2_eq};  // Bit_Extender bit_extender_2
  assign and_5_out = Data_In & bit_extender_3_out;  // AND_Gate and_5, 8 bits wide
  and and_6 (and_6_out, R_W, comparator_3_eq);
  Comparator #(.width(3), .mode("unsigned")) comparator_3 (
    .a(Address), .b(adder_2_out), .eq(comparator_3_eq));  // open: gt, lt
  assign bit_extender_3_out = {{7{comparator_3_eq}}, comparator_3_eq};  // Bit_Extender bit_extender_3
  assign and_7_out = Data_In & bit_extender_4_out;  // AND_Gate and_7, 8 bits wide
  and and_8 (and_8_out, R_W, comparator_4_eq);
  Comparator #(.width(3), .mode("unsigned")) comparator_4 (
    .a(Address), .b(adder_3_out), .eq(comparator_4_eq));  // open: gt, lt
  assign bit_extender_4_out = {{7{comparator_4_eq}}, comparator_4_eq};  // Bit_Extender bit_extender_4
  assign and_9_out = Data_In_2 & bit_extender_5_out;  // AND_Gate and_9, 8 bits wide
  and and_10 (and_10_out, R_W_2, comparator_5_eq);
  or or_1 (or_1_out, and_10_out, and_2_out);
  Comparator #(.width(3), .mode("unsigned")) comparator_5 (
    .a(Address_2), .b(3'b000), .eq(comparator_5_eq));  // open: gt, lt
  assign bit_extender_5_out = {{7{comparator_5_eq}}, comparator_5_eq};  // Bit_Extender bit_extender_5
  assign and_11_out = Data_In_2 & bit_extender_6_out;  // AND_Gate and_11, 8 bits wide
  and and_12 (and_12_out, R_W_2, comparator_6_eq);
  or or_2 (or_2_out, and_12_out, and_4_out);
  Comparator #(.width(3), .mode("unsigned")) comparator_6 (
    .a(Address_2), .b(adder_1_out), .eq(comparator_6_eq));  // open: gt, lt
  assign bit_extender_6_out = {{7{comparator_6_eq}}, comparator_6_eq};  // Bit_Extender bit_extender_6
  assign and_13_out = Data_In_2 & bit_extender_7_out;  // AND_Gate and_13, 8 bits wide
  and and_14 (and_14_out, R_W_2, comparator_7_eq);
  or or_3 (or_3_out, and_14_out, and_6_out);
  Comparator #(.width(3), .mode("unsigned")) comparator_7 (
    .a(Address_2), .b(adder_2_out), .eq(comparator_7_eq));  // open: gt, lt
  assign bit_extender_7_out = {{7{comparator_7_eq}}, comparator_7_eq};  // Bit_Extender bit_extender_7
  assign and_15_out = Data_In_2 & bit_extender_8_out;  // AND_Gate and_15, 8 bits wide
  and and_16 (and_16_out, R_W_2, comparator_8_eq);
  or or_4 (or_4_out, and_16_out, and_8_out);
  Comparator #(.width(3), .mode("unsigned")) comparator_8 (
    .a(Address_2), .b(adder_3_out), .eq(comparator_8_eq));  // open: gt, lt
  assign bit_extender_8_out = {{7{comparator_8_eq}}, comparator_8_eq};  // Bit_Extender bit_extender_8
  assign and_17_out = Data_In_3 & bit_extender_9_out;  // AND_Gate and_17, 8 bits wide
  and and_18 (and_18_out, R_W_3, comparator_9_eq);
  or or_5 (or_5_out, and_18_out, or_1_out);
  Comparator #(.width(3), .mode("unsigned")) comparator_9 (
    .a(Address_3), .b(3'b000), .eq(comparator_9_eq));  // open: gt, lt
  assign bit_extender_9_out = {{7{comparator_9_eq}}, comparator_9_eq};  // Bit_Extender bit_extender_9
  assign and_19_out = Data_In_3 & bit_extender_10_out;  // AND_Gate and_19, 8 bits wide
  and and_20 (and_20_out, R_W_3, comparator_10_eq);
  or or_6 (or_6_out, and_20_out, or_2_out);
  Comparator #(.width(3), .mode("unsigned")) comparator_10 (
    .a(Address_3), .b(adder_1_out), .eq(comparator_10_eq));  // open: gt, lt
  assign bit_extender_10_out = {{7{comparator_10_eq}}, comparator_10_eq};  // Bit_Extender bit_extender_10
  assign and_21_out = Data_In_3 & bit_extender_11_out;  // AND_Gate and_21, 8 bits wide
  and and_22 (and_22_out, R_W_3, comparator_11_eq);
  or or_7 (or_7_out, and_22_out, or_3_out);
  Comparator #(.width(3), .mode("unsigned")) comparator_11 (
    .a(Address_3), .b(adder_2_out), .eq(comparator_11_eq));  // open: gt, lt
  assign bit_extender_11_out = {{7{comparator_11_eq}}, comparator_11_eq};  // Bit_Extender bit_extender_11
  assign and_23_out = Data_In_3 & bit_extender_12_out;  // AND_Gate and_23, 8 bits wide
  and and_24 (and_24_out, R_W_3, comparator_12_eq);
  or or_8 (or_8_out, and_24_out, or_4_out);
  Comparator #(.width(3), .mode("unsigned")) comparator_12 (
    .a(Address_3), .b(adder_3_out), .eq(comparator_12_eq));  // open: gt, lt
  assign bit_extender_12_out = {{7{comparator_12_eq}}, comparator_12_eq};  // Bit_Extender bit_extender_12
  assign and_25_out = Data_In_4 & bit_extender_13_out;  // AND_Gate and_25, 8 bits wide
  and and_26 (and_26_out, R_W_4, comparator_13_eq);
  or or_9 (or_9_out, and_26_out, or_5_out);
  Comparator #(.width(3), .mode("unsigned")) comparator_13 (
    .a(Address_4), .b(3'b000), .eq(comparator_13_eq));  // open: gt, lt
  assign bit_extender_13_out = {{7{comparator_13_eq}}, comparator_13_eq};  // Bit_Extender bit_extender_13
  assign and_27_out = Data_In_4 & bit_extender_14_out;  // AND_Gate and_27, 8 bits wide
  and and_28 (and_28_out, R_W_4, comparator_14_eq);
  or or_10 (or_10_out, and_28_out, or_6_out);
  Comparator #(.width(3), .mode("unsigned")) comparator_14 (
    .a(Address_4), .b(adder_1_out), .eq(comparator_14_eq));  // open: gt, lt
  assign bit_extender_14_out = {{7{comparator_14_eq}}, comparator_14_eq};  // Bit_Extender bit_extender_14
  assign and_29_out = Data_In_4 & bit_extender_15_out;  // AND_Gate and_29, 8 bits wide
  and and_30 (and_30_out, R_W_4, comparator_15_eq);
  or or_11 (or_11_out, and_30_out, or_7_out);
  Comparator #(.width(3), .mode("unsigned")) comparator_15 (
    .a(Address_4), .b(adder_2_out), .eq(comparator_15_eq));  // open: gt, lt
  assign bit_extender_15_out = {{7{comparator_15_eq}}, comparator_15_eq};  // Bit_Extender bit_extender_15
  assign and_31_out = Data_In_4 & bit_extender_16_out;  // AND_Gate and_31, 8 bits wide
  and and_32 (and_32_out, R_W_4, comparator_16_eq);
  or or_12 (or_12_out, and_32_out, or_8_out);
  Comparator #(.width(3), .mode("unsigned")) comparator_16 (
    .a(Address_4), .b(adder_3_out), .eq(comparator_16_eq));  // open: gt, lt
  assign bit_extender_16_out = {{7{comparator_16_eq}}, comparator_16_eq};  // Bit_Extender bit_extender_16
  Clock clock_1 (.out(clock_1_out));
  assign or_13_out = and_25_out | and_17_out | and_9_out | and_1_out;  // OR_Gate or_13, 8 bits wide
  Register register_1 (.D(or_13_out), .en(or_9_out), .Q(register_1_q), .clk(clock_1_out));  // open: clr
  Register register_2 (.D(or_14_out), .en(or_10_out), .Q(register_2_q), .clk(clock_1_out));  // open: clr
  assign or_14_out = and_27_out | and_19_out | and_11_out | and_3_out;  // OR_Gate or_14, 8 bits wide
  assign or_15_out = and_29_out | and_21_out | and_13_out | and_5_out;  // OR_Gate or_15, 8 bits wide
  Register register_3 (.D(or_15_out), .en(or_11_out), .Q(register_3_q), .clk(clock_1_out));  // open: clr
  Register register_4 (.D(or_16_out), .en(or_12_out), .Q(register_4_q), .clk(clock_1_out));  // open: clr
  assign or_16_out = and_31_out | and_23_out | and_15_out | and_7_out;  // OR_Gate or_16, 8 bits wide
  Transistor #(.\type ("n"), .width(8)) transistor_1 (.in(register_1_q), .out(Data_Out_2), .gate(comparator_5_eq));
  Transistor #(.\type ("n"), .width(8)) transistor_2 (.in(register_1_q), .out(Data_Out), .gate(comparator_1_eq));
  Transistor #(.\type ("n"), .width(8)) transistor_3 (.in(register_2_q), .out(Data_Out), .gate(comparator_2_eq));
  Transistor #(.\type ("n"), .width(8)) transistor_4 (.in(register_2_q), .out(Data_Out_2), .gate(comparator_6_eq));
  Transistor #(.\type ("n"), .width(8)) transistor_5 (.in(register_3_q), .out(Data_Out_2), .gate(comparator_7_eq));
  Transistor #(.\type ("n"), .width(8)) transistor_6 (.in(register_3_q), .out(Data_Out), .gate(comparator_3_eq));
  Transistor #(.\type ("n"), .width(8)) transistor_7 (.in(register_4_q), .out(Data_Out), .gate(comparator_4_eq));
  Transistor #(.\type ("n"), .width(8)) transistor_8 (.in(register_4_q), .out(Data_Out_2), .gate(comparator_8_eq));
  Transistor #(.\type ("n"), .width(8)) transistor_9 (.in(register_1_q), .out(Data_Out_3), .gate(comparator_9_eq));
  Transistor #(.\type ("n"), .width(8)) transistor_10 (.in(register_1_q), .out(Data_Out_4), .gate(comparator_13_eq));
  Transistor #(.\type ("n"), .width(8)) transistor_11 (.in(register_2_q), .out(Data_Out_3), .gate(comparator_10_eq));
  Transistor #(.\type ("n"), .width(8)) transistor_12 (.in(register_2_q), .out(Data_Out_4), .gate(comparator_14_eq));
  Transistor #(.\type ("n"), .width(8)) transistor_13 (.in(register_3_q), .out(Data_Out_4), .gate(comparator_15_eq));
  Transistor #(.\type ("n"), .width(8)) transistor_14 (.in(register_3_q), .out(Data_Out_3), .gate(comparator_11_eq));
  Transistor #(.\type ("n"), .width(8)) transistor_15 (.in(register_4_q), .out(Data_Out_3), .gate(comparator_12_eq));
  Transistor #(.\type ("n"), .width(8)) transistor_16 (.in(register_4_q), .out(Data_Out_4), .gate(comparator_16_eq));
endmodule

module main2 (
  input  [2:0] Address,
  input  [2:0] Address_2,
  input  [2:0] Address_3,
  input  [2:0] Address_4,
  input  R_W,
  input  [7:0] Data_In,
  input  R_W_2,
  input  [7:0] Data_In_2,
  input  R_W_3,
  input  [7:0] Data_In_3,
  input  R_W_4,
  input  [7:0] Data_In_4,
  input  in_13,
  output [7:0] Data_Out,
  output [7:0] Data_Out_2,
  output [7:0] Data_Out_3,
  output [7:0] Data_Out_4
);

  wire and_1_out, and_2_out, and_3_out, and_4_out, and_5_out, and_6_out, and_7_out, and_8_out, and_9_out,
       and_10_out, and_11_out, and_12_out, and_13_out, and_14_out, and_15_out, and_16_out, and_17_out,
       and_18_out, and_19_out, and_20_out, and_21_out, and_22_out, and_23_out, and_24_out, and_25_out,
       and_26_out, and_27_out, and_28_out, and_29_out, and_30_out, and_31_out, and_32_out, clock_1_out,
       comparator_1_eq, comparator_2_eq, comparator_3_eq, comparator_4_eq, comparator_5_eq, comparator_6_eq,
       comparator_7_eq, comparator_8_eq, comparator_9_eq, comparator_10_eq, comparator_11_eq,
       comparator_12_eq, comparator_13_eq, comparator_15_eq, comparator_16_eq, or_1_out, or_2_out, or_3_out,
       or_4_out, or_5_out, or_6_out, or_7_out, or_8_out, or_9_out, or_10_out, or_11_out, or_12_out;
  wire [7:0] register_1_q, register_2_q, register_3_q, register_4_q, transistor_1_out, transistor_2_out,
       transistor_3_out, transistor_4_out;

  Transistor #(.\type ("n"), .gate("br"), .width(8)) transistor_1 (
    .in(Data_In), .out(transistor_1_out), .gate(and_2_out));
  and and_1 (and_1_out, R_W, comparator_1_eq);
  Comparator #(.width(3), .mode("unsigned")) comparator_1 (
    .a(Address), .b(3'b000), .eq(comparator_1_eq));  // open: gt, lt
  and and_2 (and_2_out, comparator_1_eq, R_W);
  Transistor #(.\type ("n"), .gate("br"), .width(8)) transistor_2 (
    .in(Data_In), .out(transistor_2_out), .gate(and_4_out));
  and and_3 (and_3_out, R_W, comparator_2_eq);
  and and_4 (and_4_out, comparator_2_eq, R_W);
  Comparator #(.width(3), .mode("unsigned")) comparator_2 (
    .a(Address), .b(3'b001), .eq(comparator_2_eq));  // open: gt, lt
  Transistor #(.\type ("n"), .gate("br"), .width(8)) transistor_3 (
    .in(Data_In), .out(transistor_3_out), .gate(and_6_out));
  and and_5 (and_5_out, R_W, comparator_3_eq);
  Comparator #(.width(3), .mode("unsigned")) comparator_3 (
    .a(Address), .b(3'b010), .eq(comparator_3_eq));  // open: gt, lt
  and and_6 (and_6_out, comparator_3_eq, R_W);
  Transistor #(.\type ("n"), .gate("br"), .width(8)) transistor_4 (
    .in(Data_In), .out(transistor_4_out), .gate(and_8_out));
  and and_7 (and_7_out, R_W, comparator_4_eq);
  Comparator #(.width(3), .mode("unsigned")) comparator_4 (
    .a(Address), .b(3'b011), .eq(comparator_4_eq));  // open: gt, lt
  and and_8 (and_8_out, comparator_4_eq, R_W);
  Transistor #(.\type ("n"), .gate("br"), .width(8)) transistor_5 (
    .in(Data_In_2), .out(transistor_1_out), .gate(and_10_out));
  and and_9 (and_9_out, R_W_2, comparator_5_eq);
  or or_1 (or_1_out, and_9_out, and_1_out);
  and and_10 (and_10_out, comparator_5_eq, R_W_2);
  Comparator #(.width(3), .mode("unsigned")) comparator_5 (
    .a(Address_2), .b(3'b000), .eq(comparator_5_eq));  // open: gt, lt
  Transistor #(.\type ("n"), .gate("br"), .width(8)) transistor_6 (
    .in(Data_In_2), .out(transistor_2_out), .gate(and_12_out));
  and and_11 (and_11_out, R_W_2, comparator_6_eq);
  or or_2 (or_2_out, and_11_out, and_3_out);
  Comparator #(.width(3), .mode("unsigned")) comparator_6 (
    .a(Address_2), .b(3'b001), .eq(comparator_6_eq));  // open: gt, lt
  and and_12 (and_12_out, comparator_6_eq, R_W_2);
  Transistor #(.\type ("n"), .gate("br"), .width(8)) transistor_7 (
    .in(Data_In_2), .out(transistor_3_out), .gate(and_14_out));
  and and_13 (and_13_out, R_W_2, comparator_7_eq);
  or or_3 (or_3_out, and_13_out, and_5_out);
  Comparator #(.width(3), .mode("unsigned")) comparator_7 (
    .a(Address_2), .b(3'b010), .eq(comparator_7_eq));  // open: gt, lt
  and and_14 (and_14_out, comparator_7_eq, R_W_2);
  Transistor #(.\type ("n"), .gate("br"), .width(8)) transistor_8 (
    .in(Data_In_2), .out(transistor_4_out), .gate(and_16_out));
  and and_15 (and_15_out, R_W_2, comparator_8_eq);
  or or_4 (or_4_out, and_15_out, and_7_out);
  Comparator #(.width(3), .mode("unsigned")) comparator_8 (
    .a(Address_2), .b(3'b011), .eq(comparator_8_eq));  // open: gt, lt
  and and_16 (and_16_out, comparator_8_eq, R_W_2);
  Transistor #(.\type ("n"), .gate("br"), .width(8)) transistor_9 (
    .in(Data_In_3), .out(transistor_1_out), .gate(and_18_out));
  and and_17 (and_17_out, R_W_3, comparator_9_eq);
  or or_5 (or_5_out, and_17_out, or_1_out);
  Comparator #(.width(3), .mode("unsigned")) comparator_9 (
    .a(Address_3), .b(3'b000), .eq(comparator_9_eq));  // open: gt, lt
  and and_18 (and_18_out, comparator_9_eq, R_W_3);
  Transistor #(.\type ("n"), .gate("br"), .width(8)) transistor_10 (
    .in(Data_In_3), .out(transistor_2_out), .gate(and_20_out));
  and and_19 (and_19_out, R_W_3, comparator_10_eq);
  or or_6 (or_6_out, and_19_out, or_2_out);
  and and_20 (and_20_out, comparator_10_eq, R_W_3);
  Comparator #(.width(3), .mode("unsigned")) comparator_10 (
    .a(Address_3), .b(3'b001), .eq(comparator_10_eq));  // open: gt, lt
  Transistor #(.\type ("n"), .gate("br"), .width(8)) transistor_11 (
    .in(Data_In_3), .out(transistor_3_out), .gate(and_22_out));
  and and_21 (and_21_out, R_W_3, comparator_11_eq);
  or or_7 (or_7_out, and_21_out, or_3_out);
  Comparator #(.width(3), .mode("unsigned")) comparator_11 (
    .a(Address_3), .b(3'b010), .eq(comparator_11_eq));  // open: gt, lt
  and and_22 (and_22_out, comparator_11_eq, R_W_3);
  Transistor #(.\type ("n"), .gate("br"), .width(8)) transistor_12 (
    .in(Data_In_3), .out(transistor_4_out), .gate(and_24_out));
  and and_23 (and_23_out, R_W_3, comparator_12_eq);
  or or_8 (or_8_out, and_23_out, or_4_out);
  and and_24 (and_24_out, comparator_12_eq, R_W_3);
  Comparator #(.width(3), .mode("unsigned")) comparator_12 (
    .a(Address_3), .b(3'b011), .eq(comparator_12_eq));  // open: gt, lt
  Transistor #(.\type ("n"), .gate("br"), .width(8)) transistor_13 (
    .in(Data_In_4), .out(transistor_1_out), .gate(and_26_out));
  and and_25 (and_25_out, R_W_4, comparator_13_eq);
  or or_9 (or_9_out, and_25_out, or_5_out);
  Comparator #(.width(3), .mode("unsigned")) comparator_13 (
    .a(Address_4), .b(3'b000), .eq(comparator_13_eq));  // open: gt, lt
  and and_26 (and_26_out, comparator_13_eq, R_W_4);
  Transistor #(.\type ("n"), .gate("br"), .width(8)) transistor_14 (
    .in(Data_In_4), .out(transistor_2_out), .gate(and_28_out));
  and and_27 (and_27_out, R_W_4, and_27_out);
  or or_10 (or_10_out, and_27_out, or_6_out);
  Comparator #(.width(3), .mode("unsigned")) comparator_14 (
    .a(Address_4), .b(3'b001), .eq(and_27_out));  // open: gt, lt
  and and_28 (and_28_out, and_27_out, R_W_4);
  Transistor #(.\type ("n"), .gate("br"), .width(8)) transistor_15 (
    .in(Data_In_4), .out(transistor_3_out), .gate(and_30_out));
  and and_29 (and_29_out, R_W_4, comparator_15_eq);
  or or_11 (or_11_out, and_29_out, or_7_out);
  and and_30 (and_30_out, comparator_15_eq, R_W_4);
  Comparator #(.width(3), .mode("unsigned")) comparator_15 (
    .a(Address_4), .b(3'b010), .eq(comparator_15_eq));  // open: gt, lt
  Transistor #(.\type ("n"), .gate("br"), .width(8)) transistor_16 (
    .in(Data_In_4), .out(transistor_4_out), .gate(and_32_out));
  and and_31 (and_31_out, R_W_4, comparator_16_eq);
  or or_12 (or_12_out, and_31_out, or_8_out);
  Comparator #(.width(3), .mode("unsigned")) comparator_16 (
    .a(Address_4), .b(3'b011), .eq(comparator_16_eq));  // open: gt, lt
  and and_32 (and_32_out, comparator_16_eq, R_W_4);
  Clock clock_1 (.out(clock_1_out));
  Register register_1 (.D(transistor_1_out), .en(or_9_out), .Q(register_1_q), .clk(clock_1_out));  // open: clr
  Register register_2 (.D(transistor_2_out), .en(or_10_out), .Q(register_2_q), .clk(clock_1_out));  // open: clr
  Register register_3 (.D(transistor_3_out), .en(or_11_out), .Q(register_3_q), .clk(clock_1_out));  // open: clr
  Register register_4 (.D(transistor_4_out), .en(or_12_out), .Q(register_4_q), .clk(clock_1_out));  // open: clr
  Transistor #(.\type ("n"), .width(8)) transistor_17 (.in(register_1_q), .out(Data_Out_2), .gate(comparator_5_eq));
  Transistor #(.\type ("n"), .width(8)) transistor_18 (.in(register_1_q), .out(Data_Out), .gate(comparator_1_eq));
  Transistor #(.\type ("n"), .width(8)) transistor_19 (.in(register_1_q), .out(Data_Out_3), .gate(comparator_9_eq));
  Transistor #(.\type ("n"), .width(8)) transistor_20 (.in(register_2_q), .out(Data_Out_2), .gate(comparator_6_eq));
  Transistor #(.\type ("n"), .width(8)) transistor_21 (.in(register_2_q), .out(Data_Out), .gate(comparator_2_eq));
  Transistor #(.\type ("n"), .width(8)) transistor_22 (.in(register_2_q), .out(Data_Out_3), .gate(comparator_10_eq));
  Transistor #(.\type ("n"), .width(8)) transistor_23 (.in(register_3_q), .out(Data_Out_2), .gate(comparator_7_eq));
  Transistor #(.\type ("n"), .width(8)) transistor_24 (.in(register_3_q), .out(Data_Out), .gate(comparator_3_eq));
  Transistor #(.\type ("n"), .width(8)) transistor_25 (.in(register_3_q), .out(Data_Out_3), .gate(comparator_11_eq));
  Transistor #(.\type ("n"), .width(8)) transistor_26 (.in(register_4_q), .out(Data_Out_3), .gate(comparator_12_eq));
  Transistor #(.\type ("n"), .width(8)) transistor_27 (.in(register_4_q), .out(Data_Out_2), .gate(comparator_8_eq));
  Transistor #(.\type ("n"), .width(8)) transistor_28 (.in(register_4_q), .out(Data_Out), .gate(comparator_4_eq));
  Transistor #(.\type ("n"), .width(8)) transistor_29 (.in(register_1_q), .out(Data_Out_4), .gate(comparator_13_eq));
  Transistor #(.\type ("n"), .width(8)) transistor_30 (.in(register_2_q), .out(Data_Out_4), .gate(and_27_out));
  Transistor #(.\type ("n"), .width(8)) transistor_31 (.in(register_3_q), .out(Data_Out_4), .gate(comparator_15_eq));
  Transistor #(.\type ("n"), .width(8)) transistor_32 (.in(register_4_q), .out(Data_Out_4), .gate(comparator_16_eq));
endmodule
