// Logisim project Multiplier.circ as structural Verilog: 8 circuits, main circuit main
module main (
  input  in_1,
  input  in_2,
  input  in_3,
  input  in_4,
  input  in_5,
  input  in_6,
  input  in_7,
  input  in_8,
  input  in_9,
  input  in_10,
  input  in_11,
  input  in_12,
  input  in_13,
  input  in_14,
  input  in_15,
  input  in_16,
  input  B3,
  input  B2,
  input  B1,
  input  B0,
  input  A0,
  input  A1,
  input  A2,
  input  A3,
  input  A3_2,
  input  A2_2,
  input  A1_2,
  input  A0_2,
  input  B3_2,
  input  B2_2,
  input  B1_2,
  input  B0_2,
  input  A3_3,
  input  A2_3,
  input  A1_3,
  input  A0_3,
  input  B3_3,
  input  B2_3,
  input  B1_3,
  input  B0_3,
  input  B3_4,
  input  B2_4,
  input  B1_4,
  input  B0_4,
  input  A3_4,
  input  A2_4,
  input  A1_4,
  input  A0_4,
  input  A3_5,
  input  A2_5,
  input  A1_5,
  input  A0_5,
  input  B3_5,
  input  B2_5,
  input  B1_5,
  input  B0_5,
  output out_57,
  output out_58,
  output out_59,
  output out_60,
  output out_61,
  output out_62,
  output out_63,
  output out_64,
  output R0,
  output R1,
  output R2,
  output R3,
  output R4,
  output R5,
  output R6,
  output R7,
  output R7_2,
  output R6_2,
  output R5_2,
  output R3_2,
  output R2_2,
  output R1_2,
  output R0_2,
  output R8,
  output R7_3,
  output R6_3,
  output R5_3,
  output R3_3,
  output R2_3,
  output R1_3,
  output R0_3,
  output R8_2,
  output R7_4,
  output R6_4,
  output R5_4,
  output R3_4,
  output R2_4,
  output R1_4,
  output R0_4,
  output R8_3,
  output R7_5,
  output R6_5,
  output R5_5,
  output R3_5,
  output R2_5,
  output R1_5,
  output R0_5
);

  wire mulbase_1_sout, mulbase_2_sout, mulbase_3_sout, mulbase_4_sout, mulbase_5_sout, mulbase_6_sout,
       mulend_2_cout, mulend_3_cout, mulful_5_cout, mulful_5_sout, mulful_6_cout, mulful_6_sout,
       mulful_7_cout, mulful_8_cout, mulful_8_sout, mulful_9_cout, mulful_9_sout, mulful_10_cout,
       mulful_10_sout, mulful_11_cout, mulful_11_sout, mulful_12_cout, mulful_12_sout, mulful_13_cout,
       mulful_13_sout, mulful_14_cout, mulful_15_cout, mulful_16_cout, mulful_16_sout, mulful_17_cout,
       mulful_17_sout, mulful_18_cout, mulful_19_cout, mulful_19_sout, mulful_20_cout, mulful_20_sout,
       mulful_21_cout, mulful_21_sout, mulful_22_cout, mulhalf_1_cout, mulhalf_1_sout, mulhalf_2_cout,
       mulhalf_2_sout, mulhalf_3_cout, multiply_1_cout, multiply_2_cout, multiply_2_sout, multiply_3_cout,
       multiply_4_cout, multiply_5_sout, multiply_6_cout, multiply_6_sout, multiply_7_sout, multiply_8_cout,
       multiply_8_sout, multiply_9_cout, multiply_10_sout, multiply_12_cout, multiply_12_sout,
       multiply_13_cout, multiply_14_cout, multiply_14_sout, multiply_15_cout, multiply_15_sout,
       multiply_16_cout, multiply_16_sout, multiply_17_cout, multiply_17_sout, multiply_18_cout,
       multiply_18_sout, multiply_19_cout, multiply_20_cout, multiply_21_cout, multiply_21_sout,
       multiply_22_cout, multiply_22_sout, multiply_23_cout, multiply_24_cout, multiply_25_cout,
       multiply_25_sout, multiply_26_cout, multiply_27_cout, multiply_29_cout, multiply_29_sout,
       multiply_30_cout, multiply_30_sout, multiply_31_cout, multiply_32_cout, multiply_33_cout,
       multiply_33_sout, multiply_39_cout, multiply_40_cout, multiply_41_cout, multiply_a_1_cout,
       multiply_a_1_out_8, multiply_a_1_s, multiply_a_2_cout, multiply_a_2_out_8, multiply_a_2_s,
       multiply_a_3_cout, multiply_a_3_out_8, multiply_a_3_s, multiply_a_4_cout, multiply_a_4_out_8,
       multiply_a_4_s, multiply_a_5_cout, multiply_a_5_out_5, multiply_a_5_out_8, multiply_a_5_s,
       multiply_a_6_cout, multiply_a_6_out_5, multiply_a_6_out_8, multiply_a_6_s, multiply_a_7_cout,
       multiply_a_7_out_5, multiply_a_7_out_8, multiply_a_7_s, multiply_a_8_cout, multiply_a_8_out_5,
       multiply_a_8_out_8, multiply_a_8_s, multiply_a_9_cout, multiply_a_9_out_5, multiply_a_9_out_8,
       multiply_a_9_s, multiply_a_10_cout, multiply_a_10_out_5, multiply_a_10_out_8, multiply_a_10_s,
       multiply_a_11_cout, multiply_a_11_out_5, multiply_a_11_out_8, multiply_a_11_s, multiply_a_12_cout,
       multiply_a_12_out_5, multiply_a_12_out_8, multiply_a_12_s, multiply_a_13_cout, multiply_a_13_out_5,
       multiply_a_13_out_8, multiply_a_14_cout, multiply_a_14_out_5, multiply_a_14_out_8, multiply_a_15_cout,
       multiply_a_15_out_5, multiply_a_15_out_8, multiply_a_16_cout, multiply_a_16_out_5,
       multiply_a_16_out_8, multiply_b_2_cout, multiply_b_3_cout, multiply_b_4_cout;

  Multiply multiply_1 (.A(in_9), .Cin(1'b0), .Cout(multiply_1_cout), .B(in_1), .Sin(1'b0), .Sout(out_57));
  Multiply multiply_2 (
    .A(in_9), .Cin(multiply_1_cout), .Cout(multiply_2_cout), .B(in_2), .Sin(1'b0), .Sout(multiply_2_sout));
  Multiply multiply_3 (.A(in_11), .Cin(1'b0), .Cout(multiply_3_cout), .B(in_2), .Sin(multiply_2_sout), .Sout(out_58));
  Multiply multiply_4 (.A(B0), .Cin(1'b0), .Cout(multiply_4_cout), .B(A0), .Sin(1'b0), .Sout(R0));
  Multiply_A multiply_a_1 (
    .A(1'b0), .in_4(multiply_a_5_out_5), .S(multiply_a_1_s), .B(1'b0), .in_2(A3_4), .Cout(multiply_a_1_cout),
    .out_8(multiply_a_1_out_8));  // open: out_5
  Multiply_A multiply_a_2 (
    .A(1'b0), .in_4(multiply_a_8_out_5), .S(multiply_a_2_s), .B(multiply_a_1_cout),
    .in_2(multiply_a_1_out_8), .Cout(multiply_a_2_cout), .out_8(multiply_a_2_out_8));  // open: out_5
  Multiply_A multiply_a_3 (
    .A(1'b0), .in_4(multiply_a_9_out_5), .S(multiply_a_3_s), .B(multiply_a_2_cout),
    .in_2(multiply_a_2_out_8), .Cout(multiply_a_3_cout), .out_8(multiply_a_3_out_8));  // open: out_5
  Multiply_A multiply_a_4 (
    .A(1'b0), .in_4(multiply_a_12_out_5), .S(multiply_a_4_s), .B(multiply_a_3_cout),
    .in_2(multiply_a_3_out_8), .Cout(multiply_a_4_cout), .out_8(multiply_a_4_out_8));  // open: out_5
  Multiply_B multiply_b_1 (
    .A(1'b0), .in_4(multiply_b_3_cout), .in_1(multiply_a_4_cout), .in_2(multiply_a_4_out_8), .S(R8_2));  // open: out_5, Cout
  Multiply multiply_5 (.A(in_9), .Cin(multiply_6_cout), .B(in_4), .Sin(1'b0), .Sout(multiply_5_sout));  // open: Cout
  Multiply multiply_6 (
    .A(in_9), .Cin(multiply_2_cout), .Cout(multiply_6_cout), .B(in_3), .Sin(1'b0), .Sout(multiply_6_sout));
  Multiply multiply_7 (
    .A(in_11), .Cin(multiply_8_cout), .B(in_4), .Sin(multiply_5_sout), .Sout(multiply_7_sout));  // open: Cout
  Multiply multiply_8 (
    .A(in_11), .Cin(multiply_3_cout), .Cout(multiply_8_cout), .B(in_3), .Sin(multiply_6_sout),
    .Sout(multiply_8_sout));
  Multiply multiply_9 (.A(in_13), .Cin(1'b0), .Cout(multiply_9_cout), .B(in_3), .Sin(multiply_8_sout), .Sout(out_59));
  Multiply multiply_10 (
    .A(in_13), .Cin(multiply_9_cout), .B(in_4), .Sin(multiply_7_sout), .Sout(multiply_10_sout));  // open: Cout
  Multiply multiply_11 (.A(in_15), .Cin(1'b0), .B(in_4), .Sin(multiply_10_sout), .Sout(out_60));  // open: Cout
  Multiply multiply_12 (
    .A(B0), .Cin(multiply_4_cout), .Cout(multiply_12_cout), .B(A1), .Sin(1'b0), .Sout(multiply_12_sout));
  Multiply multiply_13 (.A(B1), .Cin(1'b0), .Cout(multiply_13_cout), .B(A0), .Sin(multiply_12_sout), .Sout(R1));
  Multiply_A multiply_a_5 (
    .A(1'b0), .out_5(multiply_a_5_out_5), .in_4(multiply_a_6_out_5), .S(multiply_a_5_s), .B(1'b0),
    .in_2(A2_4), .Cout(multiply_a_5_cout), .out_8(multiply_a_5_out_8));
  Multiply_A multiply_a_6 (
    .A(1'b0), .out_5(multiply_a_6_out_5), .in_4(multiply_a_13_out_5), .S(multiply_a_6_s), .B(1'b0),
    .in_2(A1_4), .Cout(multiply_a_6_cout), .out_8(multiply_a_6_out_8));
  Multiply_A multiply_a_7 (
    .A(multiply_a_5_s), .out_5(multiply_a_7_out_5), .in_4(multiply_a_14_out_5), .S(multiply_a_7_s),
    .B(multiply_a_6_cout), .in_2(multiply_a_6_out_8), .Cout(multiply_a_7_cout), .out_8(multiply_a_7_out_8));
  Multiply_A multiply_a_8 (
    .A(multiply_a_1_s), .out_5(multiply_a_8_out_5), .in_4(multiply_a_7_out_5), .S(multiply_a_8_s),
    .B(multiply_a_5_cout), .in_2(multiply_a_5_out_8), .Cout(multiply_a_8_cout), .out_8(multiply_a_8_out_8));
  Multiply_A multiply_a_9 (
    .A(multiply_a_2_s), .out_5(multiply_a_9_out_5), .in_4(multiply_a_10_out_5), .S(multiply_a_9_s),
    .B(multiply_a_8_cout), .in_2(multiply_a_8_out_8), .Cout(multiply_a_9_cout), .out_8(multiply_a_9_out_8));
  Multiply_A multiply_a_10 (
    .A(multiply_a_8_s), .out_5(multiply_a_10_out_5), .in_4(multiply_a_15_out_5), .S(multiply_a_10_s),
    .B(multiply_a_7_cout), .in_2(multiply_a_7_out_8), .Cout(multiply_a_10_cout), .out_8(multiply_a_10_out_8));
  Multiply_A multiply_a_11 (
    .A(multiply_a_9_s), .out_5(multiply_a_11_out_5), .in_4(multiply_a_16_out_5), .S(multiply_a_11_s),
    .B(multiply_a_10_cout), .in_2(multiply_a_10_out_8), .Cout(multiply_a_11_cout), .out_8(multiply_a_11_out_8));
  Multiply_A multiply_a_12 (
    .A(multiply_a_3_s), .out_5(multiply_a_12_out_5), .in_4(multiply_a_11_out_5), .S(multiply_a_12_s),
    .B(multiply_a_9_cout), .in_2(multiply_a_9_out_8), .Cout(multiply_a_12_cout), .out_8(multiply_a_12_out_8));
  Multiply_B multiply_b_2 (
    .A(multiply_a_12_s), .in_4(multiply_b_4_cout), .in_1(multiply_a_11_cout), .in_2(multiply_a_11_out_8),
    .Cout(multiply_b_2_cout), .S(R6_4));  // open: out_5
  Multiply_B multiply_b_3 (
    .A(multiply_a_4_s), .in_4(multiply_b_2_cout), .in_1(multiply_a_12_cout), .in_2(multiply_a_12_out_8),
    .Cout(multiply_b_3_cout), .S(R7_4));  // open: out_5
  Multiply multiply_14 (
    .A(B0), .Cin(multiply_12_cout), .Cout(multiply_14_cout), .B(A2), .Sin(1'b0), .Sout(multiply_14_sout));
  Multiply multiply_15 (
    .A(B0), .Cin(multiply_14_cout), .Cout(multiply_15_cout), .B(A3), .Sin(1'b0), .Sout(multiply_15_sout));
  Multiply multiply_16 (
    .A(B1), .Cin(multiply_17_cout), .Cout(multiply_16_cout), .B(A2), .Sin(multiply_15_sout),
    .Sout(multiply_16_sout));
  Multiply multiply_17 (
    .A(B1), .Cin(multiply_13_cout), .Cout(multiply_17_cout), .B(A1), .Sin(multiply_14_sout),
    .Sout(multiply_17_sout));
  Multiply multiply_18 (
    .A(B2), .Cin(multiply_19_cout), .Cout(multiply_18_cout), .B(A1), .Sin(multiply_16_sout),
    .Sout(multiply_18_sout));
  Multiply multiply_19 (.A(B2), .Cin(1'b0), .Cout(multiply_19_cout), .B(A0), .Sin(multiply_17_sout), .Sout(R2));
  Multiply multiply_20 (.A(B3), .Cin(1'b0), .Cout(multiply_20_cout), .B(A0), .Sin(multiply_18_sout), .Sout(R3));
  Multiply_A multiply_a_13 (
    .A(1'b0), .out_5(multiply_a_13_out_5), .in_4(B0_4), .S(R0_4), .B(1'b0), .in_2(A0_4),
    .Cout(multiply_a_13_cout), .out_8(multiply_a_13_out_8));
  Multiply_A multiply_a_14 (
    .A(multiply_a_6_s), .out_5(multiply_a_14_out_5), .in_4(B1_4), .S(R1_4), .B(multiply_a_13_cout),
    .in_2(multiply_a_13_out_8), .Cout(multiply_a_14_cout), .out_8(multiply_a_14_out_8));
  Multiply_A multiply_a_15 (
    .A(multiply_a_7_s), .out_5(multiply_a_15_out_5), .in_4(B2_4), .S(R2_4), .B(multiply_a_14_cout),
    .in_2(multiply_a_14_out_8), .Cout(multiply_a_15_cout), .out_8(multiply_a_15_out_8));
  Multiply_A multiply_a_16 (
    .A(multiply_a_10_s), .out_5(multiply_a_16_out_5), .in_4(B3_4), .S(R3_4), .B(multiply_a_15_cout),
    .in_2(multiply_a_15_out_8), .Cout(multiply_a_16_cout), .out_8(multiply_a_16_out_8));
  Multiply_B multiply_b_4 (
    .A(multiply_a_11_s), .in_4(1'b0), .in_1(multiply_a_16_cout), .in_2(multiply_a_16_out_8),
    .Cout(multiply_b_4_cout), .S(R5_4));  // open: out_5
  Multiply multiply_21 (
    .A(B1), .Cin(multiply_16_cout), .Cout(multiply_21_cout), .B(A3), .Sin(multiply_15_cout),
    .Sout(multiply_21_sout));
  Multiply multiply_22 (
    .A(B2), .Cin(multiply_18_cout), .Cout(multiply_22_cout), .B(A2), .Sin(multiply_21_sout),
    .Sout(multiply_22_sout));
  Multiply multiply_23 (
    .A(B3), .Cin(multiply_20_cout), .Cout(multiply_23_cout), .B(A1), .Sin(multiply_22_sout), .Sout(R4));
  Multiply multiply_24 (.A(in_10), .Cin(1'b0), .Cout(multiply_24_cout), .B(in_5), .Sin(1'b0), .Sout(out_61));
  Multiply multiply_25 (
    .A(B2), .Cin(multiply_22_cout), .Cout(multiply_25_cout), .B(A3), .Sin(multiply_21_cout),
    .Sout(multiply_25_sout));
  Multiply multiply_26 (
    .A(B3), .Cin(multiply_23_cout), .Cout(multiply_26_cout), .B(A2), .Sin(multiply_25_sout), .Sout(R5));
  Multiply multiply_27 (
    .A(in_10), .Cin(multiply_24_cout), .Cout(multiply_27_cout), .B(in_6), .Sin(1'b0), .Sout(out_62));
  Multiply multiply_28 (.A(B3), .Cin(multiply_26_cout), .Cout(R7), .B(A3), .Sin(multiply_25_cout), .Sout(R6));
  Multiply multiply_29 (
    .A(in_10), .Cin(multiply_27_cout), .Cout(multiply_29_cout), .B(in_7), .Sin(1'b0), .Sout(multiply_29_sout));
  Multiply multiply_30 (
    .A(in_10), .Cin(multiply_29_cout), .Cout(multiply_30_cout), .B(in_8), .Sin(1'b0), .Sout(multiply_30_sout));
  Multiply multiply_31 (
    .A(in_12), .Cin(multiply_32_cout), .Cout(multiply_31_cout), .B(in_8), .Sin(multiply_30_sout),
    .Sout(out_64));
  Multiply multiply_32 (
    .A(in_12), .Cin(1'b0), .Cout(multiply_32_cout), .B(in_7), .Sin(multiply_29_sout), .Sout(out_63));
  Multiply multiply_33 (
    .A(in_12), .Cin(multiply_31_cout), .Cout(multiply_33_cout), .B(multiply_30_cout), .Sin(1'b0),
    .Sout(multiply_33_sout));
  Multiply multiply_34 (.A(in_14), .Cin(1'b0), .B(1'b0), .Sin(multiply_33_sout));  // open: Cout, Sout
  Multiply multiply_35 (.A(in_12), .Cin(multiply_33_cout), .B(1'b0), .Sin(1'b0));  // open: Cout, Sout
  Multiply multiply_36 (.A(in_14));  // open: Cin, Cout, B, Sin, Sout
  MulEnd mulend_1 (.A(mulbase_1_sout), .B(mulful_5_cout), .Cout(R8), .Cin(mulend_2_cout), .Sout(R7_3));
  MulEnd mulend_2 (.A(mulful_5_sout), .B(mulful_6_cout), .Cout(mulend_2_cout), .Cin(mulend_3_cout), .Sout(R6_3));
  MulEnd mulend_3 (.A(mulful_6_sout), .B(mulful_7_cout), .Cout(mulend_3_cout), .Cin(1'b0), .Sout(R5_3));
  Multiply multiply_37 (.A(in_14));  // open: Cin, Cout, B, Sin, Sout
  Multiply multiply_38 (.A(in_14));  // open: Cin, Cout, B, Sin, Sout
  Multiply multiply_39 (.A(in_16), .Cin(1'b0), .Cout(multiply_39_cout));  // open: B, Sin, Sout
  Multiply multiply_40 (.A(in_16), .Cin(multiply_39_cout), .Cout(multiply_40_cout));  // open: B, Sin, Sout
  MulFul mulful_1 (.A(B3_2), .B(A3_2), .Sin(1'b0), .Cin(mulful_9_cout), .Sout(R7_2));  // open: Cout
  MulFul mulful_2 (.A(B2_2), .B(A3_2), .Sin(mulful_9_sout), .Cin(mulful_10_cout), .Sout(R6_2));  // open: Cout
  MulFul mulful_3 (.A(B1_2), .B(A3_2), .Sin(mulful_10_sout), .Cin(mulful_12_cout), .Sout(R5_2));  // open: Cout
  MulFul mulful_4 (.A(B0_2), .B(A3_2), .Sin(mulful_12_sout), .Cin(mulful_14_cout), .Sout(R3_2));  // open: Cout
  MulBase mulbase_1 (.A(B3_3), .B(A3_3), .Sout(mulbase_1_sout));
  MulFul mulful_5 (
    .A(B2_3), .B(A3_3), .Sin(mulbase_2_sout), .Cout(mulful_5_cout), .Cin(mulful_16_cout), .Sout(mulful_5_sout));
  MulFul mulful_6 (
    .A(B1_3), .B(A3_3), .Sin(mulful_16_sout), .Cout(mulful_6_cout), .Cin(mulful_17_cout), .Sout(mulful_6_sout));
  MulFul mulful_7 (.A(B0_3), .B(A3_3), .Sin(mulful_17_sout), .Cout(mulful_7_cout), .Cin(mulful_18_cout), .Sout(R3_3));
  Multiply multiply_41 (.A(in_16), .Cin(multiply_40_cout), .Cout(multiply_41_cout));  // open: B, Sin, Sout
  MulFul mulful_8 (.A(B3_2), .B(A1_2), .Sin(1'b0), .Cout(mulful_8_cout), .Cin(mulful_19_cout), .Sout(mulful_8_sout));
  MulFul mulful_9 (.A(B3_2), .B(A2_2), .Sin(1'b0), .Cout(mulful_9_cout), .Cin(mulful_8_cout), .Sout(mulful_9_sout));
  MulFul mulful_10 (
    .A(B2_2), .B(A2_2), .Sin(mulful_8_sout), .Cout(mulful_10_cout), .Cin(mulful_11_cout),
    .Sout(mulful_10_sout));
  MulFul mulful_11 (
    .A(B2_2), .B(A1_2), .Sin(mulful_19_sout), .Cout(mulful_11_cout), .Cin(mulful_20_cout),
    .Sout(mulful_11_sout));
  MulFul mulful_12 (
    .A(B1_2), .B(A2_2), .Sin(mulful_11_sout), .Cout(mulful_12_cout), .Cin(mulful_13_cout),
    .Sout(mulful_12_sout));
  MulFul mulful_13 (
    .A(B1_2), .B(A1_2), .Sin(mulful_20_sout), .Cout(mulful_13_cout), .Cin(mulful_21_cout),
    .Sout(mulful_13_sout));
  MulFul mulful_14 (.A(B0_2), .B(A2_2), .Sin(mulful_13_sout), .Cout(mulful_14_cout), .Cin(mulful_15_cout), .Sout(R2_2));
  MulFul mulful_15 (.A(B0_2), .B(A1_2), .Sin(mulful_21_sout), .Cout(mulful_15_cout), .Cin(mulful_22_cout), .Sout(R1_2));
  MulBase mulbase_2 (.A(B3_3), .B(A2_3), .Sout(mulbase_2_sout));
  MulBase mulbase_3 (.A(B3_3), .B(A1_3), .Sout(mulbase_3_sout));
  MulHalf mulhalf_1 (.Cout(mulhalf_1_cout), .Sin(mulbase_4_sout), .A(B2_3), .B(A1_3), .Sout(mulhalf_1_sout));
  MulFul mulful_16 (
    .A(B2_3), .B(A2_3), .Sin(mulbase_3_sout), .Cout(mulful_16_cout), .Cin(mulhalf_1_cout),
    .Sout(mulful_16_sout));
  MulHalf mulhalf_2 (.Cout(mulhalf_2_cout), .Sin(mulbase_5_sout), .A(B1_3), .B(A1_3), .Sout(mulhalf_2_sout));
  MulFul mulful_17 (
    .A(B1_3), .B(A2_3), .Sin(mulhalf_1_sout), .Cout(mulful_17_cout), .Cin(mulhalf_2_cout),
    .Sout(mulful_17_sout));
  MulHalf mulhalf_3 (.Cout(mulhalf_3_cout), .Sin(mulbase_6_sout), .A(B0_3), .B(A1_3), .Sout(R1_3));
  MulFul mulful_18 (.A(B0_3), .B(A2_3), .Sin(mulhalf_2_sout), .Cout(mulful_18_cout), .Cin(mulhalf_3_cout), .Sout(R2_3));
  Multiply multiply_42 (.A(in_16), .Cin(multiply_41_cout));  // open: Cout, B, Sin, Sout
  MulFul mulful_19 (.A(B3_2), .B(A0_2), .Sin(1'b0), .Cout(mulful_19_cout), .Cin(1'b0), .Sout(mulful_19_sout));
  MulFul mulful_20 (.A(B2_2), .B(A0_2), .Sin(1'b0), .Cout(mulful_20_cout), .Cin(1'b0), .Sout(mulful_20_sout));
  MulFul mulful_21 (.A(B1_2), .B(A0_2), .Sin(1'b0), .Cout(mulful_21_cout), .Cin(1'b0), .Sout(mulful_21_sout));
  MulFul mulful_22 (.A(B0_2), .B(A0_2), .Sin(1'b0), .Cout(mulful_22_cout), .Cin(1'b0), .Sout(R0_2));
  MulBase mulbase_4 (.A(B3_3), .B(A0_3), .Sout(mulbase_4_sout));
  MulBase mulbase_5 (.A(B2_3), .B(A0_3), .Sout(mulbase_5_sout));
  MulBase mulbase_6 (.A(B1_3), .B(A0_3), .Sout(mulbase_6_sout));
  MulBase mulbase_7 (.A(B0_3), .B(A0_3), .Sout(R0_3));

  // Notes on the sheet:
  //   Fail
  //   Fail
endmodule

module Multiply (
  input  B,
  input  Sin,
  input  A,
  input  Cin,
  output Cout,
  output Sout
);

  wire and_1_out;

  and and_1 (and_1_out, A, B);
  Adder #(.width(1)) adder_1 (.a(and_1_out), .b(Sin), .out(Sout), .cin(Cin), .cout(Cout));
endmodule

module Multiply_A (
  input  B,
  input  in_2,
  input  A,
  input  in_4,
  output out_5,
  output S,
  output Cout,
  output out_8
);

  wire and_1_out;

  and and_1 (and_1_out, in_2, in_4);
  Adder #(.width(1)) adder_1 (.a(B), .b(A), .out(S), .cin(and_1_out), .cout(Cout));

  assign out_5 = in_4;
  assign out_8 = in_2;
endmodule

module Multiply_B (
  input  in_1,
  input  in_2,
  input  A,
  input  in_4,
  output out_5,
  output Cout,
  output S
);

  wire and_1_out;

  and and_1 (and_1_out, in_2, in_4);
  Adder #(.width(1)) adder_1 (.a(in_1), .b(A), .out(S), .cin(and_1_out), .cout(Cout));

  assign out_5 = in_4;
endmodule

module MulFul (
  input  A,
  input  B,
  input  Sin,
  input  Cin,
  output Cout,
  output Sout
);

  wire and_1_out, and_2_out, and_3_out, xor_1_out;

  or or_1 (Cout, and_2_out, and_3_out);
  and and_1 (and_1_out, B, A);
  and and_2 (and_2_out, and_1_out, Sin);
  xor xor_1 (xor_1_out, Sin, and_1_out);
  and and_3 (and_3_out, Cin, xor_1_out);
  xor xor_2 (Sout, xor_1_out, Cin);
endmodule

module MulHalf (
  input  A,
  input  B,
  input  Sin,
  output Cout,
  output Sout
);

  wire and_1_out;

  and and_1 (and_1_out, B, A);
  and and_2 (Cout, and_1_out, Sin);
  xor xor_1 (Sout, Sin, and_1_out);
endmodule

module MulBase (
  input  A,
  input  B,
  output Sout
);

  and and_1 (Sout, A, B);
endmodule

module MulEnd (
  input  A,
  input  B,
  input  Cin,
  output Cout,
  output Sout
);

  wire and_1_out, and_2_out, xor_1_out;

  or or_1 (Cout, and_1_out, and_2_out);
  and and_1 (and_1_out, A, B);
  xor xor_1 (xor_1_out, B, A);
  and and_2 (and_2_out, Cin, xor_1_out);
  xor xor_2 (Sout, xor_1_out, Cin);
endmodule
