// Logisim project MultiplierV2.circ as structural Verilog: 9 circuits, main circuit main
module main (
  input  in_1,
  input  in_2,
  input  in_3,
  input  in_4,
  input  in_5,
  input  in_6,
  input  in_7,
  input  in_8,
  input  in_9,
  input  in_10,
  input  in_11,
  input  in_12,
  input  in_13,
  input  in_14,
  input  in_15,
  input  in_16,
  input  in_17,
  input  in_18,
  input  in_19,
  input  in_20,
  input  in_21,
  input  in_22,
  input  in_23,
  input  in_24,
  output out_25,
  output out_26,
  output out_27,
  output out_28,
  output out_29,
  output out_30,
  output out_31,
  output out_32,
  output out_33,
  output out_34,
  output out_35,
  output out_36,
  output out_37,
  output out_38,
  output out_39,
  output out_40,
  output out_41,
  output out_42,
  output out_43,
  output out_44,
  output out_45,
  output out_46,
  output out_47,
  output out_48
);

  wire and2_1_sout, and2_2_sout, and2_3_sout, and_1_sout, and_2_sout, and_3_sout, mul2ndhalf2_1_cout,
       mul2ndhalf2_1_sout, mul2ndhalf_1_cout, mul2ndhalf_1_sout, mulfull2_1_cout, mulfull2_1_sout,
       mulfull2_3_cout, mulfull2_3_sout, mulfull2_4_cout, mulfull2_4_sout, mulfull2_5_cout, mulfull2_6_cout,
       mulfull2_6_sout, mulfull2_7_cout, mulfull2_7_sout, mulfull2_8_cout, mulhalf2_1_cout, mulhalf2_2_cout,
       mulhalf2_3_cout, mulhalf_1_cout, mulhalf_2_cout, mulhalf_3_cout, mullfull1_1_cout, mullfull1_1_sout,
       mullfull1_2_cout, mullfull1_2_sout, mullfull1_3_cout, mullfull1_3_sout, mullfull1_5_cout,
       mullfull1_5_sout, mullfull1_7_cout, mullfull1_7_sout, mullfull1_8_cout, mullfull1_8_sout,
       mullfull1_9_cout, mullfull1_9_sout, mullfull1_10_cout, mullfull1_11_cout, mullfull1_11_sout,
       mullfull1_12_cout, mullfull1_12_sout, mullfull1_13_cout, mullfull1_14_cout, mullfull1_14_sout,
       mullfull1_15_cout, mullfull1_16_cout, mullfull1_16_sout, mullfull1_17_cout, mullfull1_18_cout,
       mullfull1_19_cout, mullfull1_19_sout, mullfull1_20_cout, mullfull1_21_cout, mullfull1_22_cout,
       mullfull1_22_sout, mullfull1_23_cout, mullfull1_23_sout, mullfull1_24_cout;

  MullFull1 mullfull1_1 (
    .Cout(mullfull1_1_cout), .B(in_5), .Cin(mullfull1_7_cout), .A(in_4), .Sin(1'b0), .Sout(mullfull1_1_sout));
  MullFull1 mullfull1_2 (
    .Cout(mullfull1_2_cout), .B(in_5), .Cin(mullfull1_8_cout), .A(in_3), .Sin(mullfull1_1_cout),
    .Sout(mullfull1_2_sout));
  MullFull1 mullfull1_3 (
    .Cout(mullfull1_3_cout), .B(in_5), .Cin(mullfull1_9_cout), .A(in_2), .Sin(mullfull1_2_cout),
    .Sout(mullfull1_3_sout));
  MullFull1 mullfull1_4 (
    .Cout(out_25), .B(in_5), .Cin(mullfull1_10_cout), .A(in_1), .Sin(mullfull1_3_cout), .Sout(out_26));
  AND and_1 (.B(in_13), .A(in_12), .Sout(and_1_sout));
  Mul2ndHalf mul2ndhalf_1 (
    .Cout(mul2ndhalf_1_cout), .B(in_13), .Cin(mullfull1_11_cout), .A(in_11), .Sout(mul2ndhalf_1_sout));
  MullFull1 mullfull1_5 (
    .Cout(mullfull1_5_cout), .B(in_13), .Cin(mullfull1_12_cout), .A(in_10), .Sin(mul2ndhalf_1_cout),
    .Sout(mullfull1_5_sout));
  MullFull1 mullfull1_6 (
    .Cout(out_33), .B(in_13), .Cin(mullfull1_13_cout), .A(in_9), .Sin(mullfull1_5_cout), .Sout(out_34));
  AND2 and2_1 (.B(in_21), .A(in_20), .Sout(and2_1_sout));
  Mul2ndHalf2 mul2ndhalf2_1 (
    .Cout(mul2ndhalf2_1_cout), .B(in_21), .Cin(mulfull2_3_cout), .A(in_19), .Sout(mul2ndhalf2_1_sout));
  MulFull2 mulfull2_1 (
    .Cout(mulfull2_1_cout), .B(in_21), .Cin(mulfull2_4_cout), .Sin(mul2ndhalf2_1_cout), .A(in_18),
    .Sout(mulfull2_1_sout));
  MulFull2 mulfull2_2 (
    .Cout(out_41), .B(in_21), .Cin(mulfull2_5_cout), .Sin(mulfull2_1_cout), .A(in_17), .Sout(out_42));
  MullFull1 mullfull1_7 (
    .Cout(mullfull1_7_cout), .B(in_6), .Cin(mullfull1_14_cout), .A(in_4), .Sin(1'b0), .Sout(mullfull1_7_sout));
  MullFull1 mullfull1_8 (
    .Cout(mullfull1_8_cout), .B(in_6), .Cin(mullfull1_16_cout), .A(in_3), .Sin(mullfull1_1_sout),
    .Sout(mullfull1_8_sout));
  MullFull1 mullfull1_9 (
    .Cout(mullfull1_9_cout), .B(in_6), .Cin(mullfull1_19_cout), .A(in_2), .Sin(mullfull1_2_sout),
    .Sout(mullfull1_9_sout));
  MullFull1 mullfull1_10 (
    .Cout(mullfull1_10_cout), .B(in_6), .Cin(mullfull1_21_cout), .A(in_1), .Sin(mullfull1_3_sout),
    .Sout(out_27));
  AND and_2 (.B(in_14), .A(in_12), .Sout(and_2_sout));
  MullFull1 mullfull1_11 (
    .Cout(mullfull1_11_cout), .B(in_14), .Cin(mullfull1_22_cout), .A(in_11), .Sin(and_1_sout),
    .Sout(mullfull1_11_sout));
  MullFull1 mullfull1_12 (
    .Cout(mullfull1_12_cout), .B(in_14), .Cin(mullfull1_23_cout), .A(in_10), .Sin(mul2ndhalf_1_sout),
    .Sout(mullfull1_12_sout));
  MullFull1 mullfull1_13 (
    .Cout(mullfull1_13_cout), .B(in_14), .Cin(mullfull1_24_cout), .A(in_9), .Sin(mullfull1_5_sout),
    .Sout(out_35));
  AND2 and2_2 (.B(in_22), .A(in_20), .Sout(and2_2_sout));
  MulFull2 mulfull2_3 (
    .Cout(mulfull2_3_cout), .B(in_22), .Cin(mulfull2_6_cout), .Sin(and2_1_sout), .A(in_19),
    .Sout(mulfull2_3_sout));
  MulFull2 mulfull2_4 (
    .Cout(mulfull2_4_cout), .B(in_22), .Cin(mulfull2_7_cout), .Sin(mul2ndhalf2_1_sout), .A(in_18),
    .Sout(mulfull2_4_sout));
  MulFull2 mulfull2_5 (
    .Cout(mulfull2_5_cout), .B(in_22), .Cin(mulfull2_8_cout), .Sin(mulfull2_1_sout), .A(in_17), .Sout(out_43));
  MullFull1 mullfull1_14 (
    .Cout(mullfull1_14_cout), .B(in_7), .Cin(mullfull1_15_cout), .A(in_4), .Sin(1'b0),
    .Sout(mullfull1_14_sout));
  MullFull1 mullfull1_15 (.Cout(mullfull1_15_cout), .B(in_8), .Cin(1'b0), .A(in_4), .Sin(1'b0), .Sout(out_32));
  MullFull1 mullfull1_16 (
    .Cout(mullfull1_16_cout), .B(in_7), .Cin(mullfull1_17_cout), .A(in_3), .Sin(mullfull1_7_sout),
    .Sout(mullfull1_16_sout));
  MullFull1 mullfull1_17 (
    .Cout(mullfull1_17_cout), .B(in_8), .Cin(1'b0), .A(in_3), .Sin(mullfull1_14_sout), .Sout(out_31));
  MullFull1 mullfull1_18 (
    .Cout(mullfull1_18_cout), .B(in_8), .Cin(1'b0), .A(in_2), .Sin(mullfull1_16_sout), .Sout(out_30));
  MullFull1 mullfull1_19 (
    .Cout(mullfull1_19_cout), .B(in_7), .Cin(mullfull1_18_cout), .A(in_2), .Sin(mullfull1_8_sout),
    .Sout(mullfull1_19_sout));
  MullFull1 mullfull1_20 (
    .Cout(mullfull1_20_cout), .B(in_8), .Cin(1'b0), .A(in_1), .Sin(mullfull1_19_sout), .Sout(out_29));
  MullFull1 mullfull1_21 (
    .Cout(mullfull1_21_cout), .B(in_7), .Cin(mullfull1_20_cout), .A(in_1), .Sin(mullfull1_9_sout),
    .Sout(out_28));
  AND and_3 (.B(in_15), .A(in_12), .Sout(and_3_sout));
  AND and_4 (.B(in_16), .A(in_12), .Sout(out_40));
  MullFull1 mullfull1_22 (
    .Cout(mullfull1_22_cout), .B(in_15), .Cin(mulhalf_1_cout), .A(in_11), .Sin(and_2_sout),
    .Sout(mullfull1_22_sout));
  MulHalf mulhalf_1 (.Cout(mulhalf_1_cout), .B(in_16), .Sin(and_3_sout), .A(in_11), .Sout(out_39));
  MullFull1 mullfull1_23 (
    .Cout(mullfull1_23_cout), .B(in_15), .Cin(mulhalf_2_cout), .A(in_10), .Sin(mullfull1_11_sout),
    .Sout(mullfull1_23_sout));
  MulHalf mulhalf_2 (.Cout(mulhalf_2_cout), .B(in_16), .Sin(mullfull1_22_sout), .A(in_10), .Sout(out_38));
  MulHalf mulhalf_3 (.Cout(mulhalf_3_cout), .B(in_16), .Sin(mullfull1_23_sout), .A(in_9), .Sout(out_37));
  MullFull1 mullfull1_24 (
    .Cout(mullfull1_24_cout), .B(in_15), .Cin(mulhalf_3_cout), .A(in_9), .Sin(mullfull1_12_sout),
    .Sout(out_36));
  AND2 and2_3 (.B(in_23), .A(in_20), .Sout(and2_3_sout));
  MulFull2 mulfull2_6 (
    .Cout(mulfull2_6_cout), .B(in_23), .Cin(mulhalf2_1_cout), .Sin(and2_2_sout), .A(in_19),
    .Sout(mulfull2_6_sout));
  MulFull2 mulfull2_7 (
    .Cout(mulfull2_7_cout), .B(in_23), .Cin(mulhalf2_2_cout), .Sin(mulfull2_3_sout), .A(in_18),
    .Sout(mulfull2_7_sout));
  MulFull2 mulfull2_8 (
    .Cout(mulfull2_8_cout), .B(in_23), .Cin(mulhalf2_3_cout), .Sin(mulfull2_4_sout), .A(in_17), .Sout(out_44));
  AND2 and2_4 (.B(in_24), .A(in_20), .Sout(out_48));
  MulHalf2 mulhalf2_1 (.Cout(mulhalf2_1_cout), .B(in_24), .Sin(and2_3_sout), .A(in_19), .Sout(out_47));
  MulHalf2 mulhalf2_2 (.Cout(mulhalf2_2_cout), .B(in_24), .Sin(mulfull2_6_sout), .A(in_18), .Sout(out_46));
  MulHalf2 mulhalf2_3 (.Cout(mulhalf2_3_cout), .B(in_24), .Sin(mulfull2_7_sout), .A(in_17), .Sout(out_45));
endmodule

module MullFull1 (
  input  Sin,
  input  A,
  input  B,
  input  Cin,
  output Cout,
  output Sout
);

  wire and_1_out, and_2_out, and_3_out, xor_1_out;

  and and_1 (and_1_out, Sin, and_3_out);
  or or_1 (Cout, and_1_out, and_2_out);
  and and_2 (and_2_out, Cin, xor_1_out);
  and and_3 (and_3_out, A, B);
  xor xor_1 (xor_1_out, and_3_out, Sin);
  xor xor_2 (Sout, xor_1_out, Cin);
endmodule

module AND (
  input  A,
  input  B,
  output Sout
);

  and and_1 (Sout, A, B);
endmodule

module MulHalf (
  input  Sin,
  input  A,
  input  B,
  output Cout,
  output Sout
);

  wire and_2_out;

  and and_1 (Cout, Sin, and_2_out);
  and and_2 (and_2_out, A, B);
  xor xor_1 (Sout, and_2_out, Sin);
endmodule

module Mul2ndHalf (
  input  A,
  input  B,
  input  Cin,
  output Cout,
  output Sout
);

  wire and_2_out;

  and and_1 (Cout, Cin, and_2_out);
  and and_2 (and_2_out, A, B);
  xor xor_1 (Sout, and_2_out, Cin);
endmodule

module MulFull2 (
  input  Sin,
  input  A,
  input  B,
  input  Cin,
  output Cout,
  output Sout
);

  wire and_1_out, and_2_out, and_3_out, xor_1_out;

  and and_1 (and_1_out, Sin, and_3_out);
  or or_1 (Cout, and_1_out, and_2_out);
  and and_2 (and_2_out, Cin, xor_1_out);
  and and_3 (and_3_out, A, B);
  xor xor_1 (xor_1_out, and_3_out, Sin);
  xor xor_2 (Sout, xor_1_out, Cin);
endmodule

module AND2 (
  input  A,
  input  B,
  output Sout
);

  and and_1 (Sout, A, B);
endmodule

module MulHalf2 (
  input  Sin,
  input  A,
  input  B,
  output Cout,
  output Sout
);

  wire and_2_out;

  and and_1 (Cout, Sin, and_2_out);
  and and_2 (and_2_out, A, B);
  xor xor_1 (Sout, and_2_out, Sin);
endmodule

module Mul2ndHalf2 (
  input  A,
  input  B,
  input  Cin,
  output Cout,
  output Sout
);

  wire and_2_out;

  and and_1 (Cout, Cin, and_2_out);
  and and_2 (and_2_out, A, B);
  xor xor_1 (Sout, and_2_out, Cin);
endmodule
