// Logisim project Pong.circ as structural Verilog: 6 circuits, main circuit main
module main (
  input  in_1
);

  wire and_3_out, and_4_out, clock_1_out, comparator_1_gt, comparator_2_gt, comparator_3_gt, comparator_4_gt,
       or_1_out, or_2_out, reset_clock_controler_1_out_3, reset_clock_controler_1_out_4,
       reset_clock_controler_1_out_5, reset_clock_controler_1_out_6;
  wire [6:0] keyboard_1_data;
  wire [15:0] and_1_out, and_2_out, bit_extender_1_out, paddle_controler_1_out_7, paddle_controler_2_out_7,
       screen_cursor_1_out_4, screen_cursor_1_out_5, screen_cursor_1_out_6, screen_cursor_1_out_7,
       screen_cursor_1_out_8, screen_cursor_1_out_9, screen_cursor_1_out_10, screen_cursor_1_out_11,
       screen_cursor_1_out_12, screen_cursor_1_out_13, screen_cursor_1_out_14, screen_cursor_1_out_15,
       screen_cursor_1_out_16, screen_cursor_1_out_17, screen_cursor_1_out_18, screen_cursor_1_out_19,
       screen_cursor_1_out_20, screen_cursor_1_out_21, screen_cursor_1_out_22, screen_cursor_1_out_23,
       screen_cursor_1_out_24, screen_cursor_1_out_25, screen_cursor_1_out_26, screen_cursor_1_out_27,
       screen_cursor_1_out_28, screen_cursor_1_out_29, screen_cursor_1_out_30, screen_cursor_1_out_31,
       screen_cursor_1_out_32, screen_cursor_1_out_33;
  wire [31:0] shift_32_back_forth_1_out_7, shift_32_back_forth_2_out_7;

  Clock clock_1 (.out(clock_1_out));
  or or_1 (or_1_out, in_1, or_2_out);
  Reset_Clock_controler reset_clock_controler_1 (
    .in_1(clock_1_out), .in_2(or_1_out), .out_5(reset_clock_controler_1_out_5),
    .out_6(reset_clock_controler_1_out_6), .out_3(reset_clock_controler_1_out_3),
    .out_4(reset_clock_controler_1_out_4));
  Keyboard keyboard_1 (.clk(reset_clock_controler_1_out_3), .re(1'b1), .data(keyboard_1_data));  // open: clr, avail
  Shift_32_Back_Forth shift_32_back_forth_1 (
    .in_1(reset_clock_controler_1_out_5), .in_3(reset_clock_controler_1_out_6),
    .in_4(reset_clock_controler_1_out_4), .in_5(32'h40000000), .in_6(32'h2),
    .out_7(shift_32_back_forth_1_out_7), .in_2(5'b10000));
  paddle_controler paddle_controler_1 (
    .in_1(reset_clock_controler_1_out_5), .in_2(reset_clock_controler_1_out_6),
    .in_3(reset_clock_controler_1_out_3), .in_4(keyboard_1_data), .in_5(7'b1110111), .in_6(7'b1110011),
    .out_7(paddle_controler_1_out_7));
  DotMatrix #(.matrixcols(32), .matrixrows(16)) dotmatrix_1 (
    .col0(paddle_controler_1_out_7), .col1(screen_cursor_1_out_19), .col2(screen_cursor_1_out_4),
    .col3(screen_cursor_1_out_20), .col4(screen_cursor_1_out_5), .col5(screen_cursor_1_out_21),
    .col6(screen_cursor_1_out_6), .col7(screen_cursor_1_out_22), .col8(screen_cursor_1_out_7),
    .col9(screen_cursor_1_out_23), .col10(screen_cursor_1_out_8), .col11(screen_cursor_1_out_24),
    .col12(screen_cursor_1_out_9), .col13(screen_cursor_1_out_25), .col14(screen_cursor_1_out_10),
    .col15(screen_cursor_1_out_26), .col16(screen_cursor_1_out_11), .col17(screen_cursor_1_out_27),
    .col18(screen_cursor_1_out_12), .col19(screen_cursor_1_out_28), .col20(screen_cursor_1_out_13),
    .col21(screen_cursor_1_out_29), .col22(screen_cursor_1_out_14), .col23(screen_cursor_1_out_30),
    .col24(screen_cursor_1_out_15), .col25(screen_cursor_1_out_31), .col26(screen_cursor_1_out_16),
    .col27(screen_cursor_1_out_32), .col28(screen_cursor_1_out_17), .col29(screen_cursor_1_out_33),
    .col30(screen_cursor_1_out_18), .col31(paddle_controler_2_out_7));
  paddle_controler paddle_controler_2 (
    .in_1(reset_clock_controler_1_out_5), .in_2(reset_clock_controler_1_out_6),
    .in_3(reset_clock_controler_1_out_3), .in_4(keyboard_1_data), .in_5(7'b1101111), .in_6(7'b1101100),
    .out_7(paddle_controler_2_out_7));
  assign and_1_out = screen_cursor_1_out_19 & paddle_controler_1_out_7;  // AND_Gate and_1, 16 bits wide
  Comparator #(.width(16), .mode("unsigned")) comparator_1 (
    .a(and_1_out), .b({16{1'b0}}), .gt(comparator_1_gt));  // open: eq, lt
  Comparator #(.width(16), .mode("unsigned")) comparator_2 (
    .a(screen_cursor_1_out_19), .b({16{1'b0}}), .gt(comparator_2_gt));  // open: eq, lt
  assign and_2_out = paddle_controler_2_out_7 & screen_cursor_1_out_18;  // AND_Gate and_2, 16 bits wide
  Comparator #(.width(16), .mode("unsigned")) comparator_3 (
    .a(and_2_out), .b({16{1'b0}}), .gt(comparator_3_gt));  // open: eq, lt
  Comparator #(.width(16), .mode("unsigned")) comparator_4 (
    .a(screen_cursor_1_out_18), .b({16{1'b0}}), .gt(comparator_4_gt));  // open: eq, lt
  and and_3 (and_3_out, ~comparator_1_gt, comparator_2_gt);  // AND_Gate
  and and_4 (and_4_out, ~comparator_3_gt, comparator_4_gt);  // AND_Gate
  Screen_Cursor screen_cursor_1 (
    .out_19(screen_cursor_1_out_19), .out_4(screen_cursor_1_out_4), .out_20(screen_cursor_1_out_20),
    .out_5(screen_cursor_1_out_5), .out_21(screen_cursor_1_out_21), .out_6(screen_cursor_1_out_6),
    .out_22(screen_cursor_1_out_22), .out_7(screen_cursor_1_out_7), .out_23(screen_cursor_1_out_23),
    .out_8(screen_cursor_1_out_8), .out_24(screen_cursor_1_out_24), .out_9(screen_cursor_1_out_9),
    .out_25(screen_cursor_1_out_25), .out_10(screen_cursor_1_out_10), .out_26(screen_cursor_1_out_26),
    .out_11(screen_cursor_1_out_11), .out_27(screen_cursor_1_out_27), .out_12(screen_cursor_1_out_12),
    .out_28(screen_cursor_1_out_28), .out_13(screen_cursor_1_out_13), .out_29(screen_cursor_1_out_29),
    .out_14(screen_cursor_1_out_14), .out_30(screen_cursor_1_out_30), .out_15(screen_cursor_1_out_15),
    .out_31(screen_cursor_1_out_31), .out_16(screen_cursor_1_out_16), .out_32(screen_cursor_1_out_32),
    .out_17(screen_cursor_1_out_17), .out_33(screen_cursor_1_out_33), .out_18(screen_cursor_1_out_18),
    .in_2(shift_32_back_forth_1_out_7), .in_1(bit_extender_1_out));  // open: out_3, out_34
  or or_2 (or_2_out, and_3_out, and_4_out);
  Shift_32_Back_Forth shift_32_back_forth_2 (
    .in_1(reset_clock_controler_1_out_5), .in_3(reset_clock_controler_1_out_6),
    .in_4(reset_clock_controler_1_out_4), .in_5(32'h8000), .in_6(32'h1), .out_7(shift_32_back_forth_2_out_7),
    .in_2(5'b00100));
  Bit_Extender #(.in_width(32)) bit_extender_1 (.in(shift_32_back_forth_2_out_7), .out(bit_extender_1_out));
endmodule

module Screen_Cursor (
  input  [15:0] in_1,
  input  [31:0] in_2,
  output [15:0] out_3,
  output [15:0] out_4,
  output [15:0] out_5,
  output [15:0] out_6,
  output [15:0] out_7,
  output [15:0] out_8,
  output [15:0] out_9,
  output [15:0] out_10,
  output [15:0] out_11,
  output [15:0] out_12,
  output [15:0] out_13,
  output [15:0] out_14,
  output [15:0] out_15,
  output [15:0] out_16,
  output [15:0] out_17,
  output [15:0] out_18,
  output [15:0] out_19,
  output [15:0] out_20,
  output [15:0] out_21,
  output [15:0] out_22,
  output [15:0] out_23,
  output [15:0] out_24,
  output [15:0] out_25,
  output [15:0] out_26,
  output [15:0] out_27,
  output [15:0] out_28,
  output [15:0] out_29,
  output [15:0] out_30,
  output [15:0] out_31,
  output [15:0] out_32,
  output [15:0] out_33,
  output [15:0] out_34
);

  And_16_1 and_16_1_1 (.out_3(out_3), .in_2(in_2[31]), .in_1(in_1));
  And_16_1 and_16_1_2 (.out_3(out_4), .in_2(in_2[29]), .in_1(in_1));
  And_16_1 and_16_1_3 (.out_3(out_19), .in_2(in_2[30]), .in_1(in_1));
  And_16_1 and_16_1_4 (.out_3(out_5), .in_2(in_2[27]), .in_1(in_1));
  And_16_1 and_16_1_5 (.out_3(out_20), .in_2(in_2[28]), .in_1(in_1));
  And_16_1 and_16_1_6 (.out_3(out_6), .in_2(in_2[25]), .in_1(in_1));
  And_16_1 and_16_1_7 (.out_3(out_22), .in_2(in_2[24]), .in_1(in_1));
  And_16_1 and_16_1_8 (.out_3(out_21), .in_2(in_2[26]), .in_1(in_1));
  And_16_1 and_16_1_9 (.out_3(out_7), .in_2(in_2[23]), .in_1(in_1));
  And_16_1 and_16_1_10 (.out_3(out_8), .in_2(in_2[21]), .in_1(in_1));
  And_16_1 and_16_1_11 (.out_3(out_23), .in_2(in_2[22]), .in_1(in_1));
  And_16_1 and_16_1_12 (.out_3(out_9), .in_2(in_2[19]), .in_1(in_1));
  And_16_1 and_16_1_13 (.out_3(out_24), .in_2(in_2[20]), .in_1(in_1));
  And_16_1 and_16_1_14 (.out_3(out_10), .in_2(in_2[17]), .in_1(in_1));
  And_16_1 and_16_1_15 (.out_3(out_26), .in_2(in_2[16]), .in_1(in_1));
  And_16_1 and_16_1_16 (.out_3(out_25), .in_2(in_2[18]), .in_1(in_1));
  And_16_1 and_16_1_17 (.out_3(out_12), .in_2(in_2[13]), .in_1(in_1));
  And_16_1 and_16_1_18 (.out_3(out_11), .in_2(in_2[15]), .in_1(in_1));
  And_16_1 and_16_1_19 (.out_3(out_27), .in_2(in_2[14]), .in_1(in_1));
  And_16_1 and_16_1_20 (.out_3(out_13), .in_2(in_2[11]), .in_1(in_1));
  And_16_1 and_16_1_21 (.out_3(out_28), .in_2(in_2[12]), .in_1(in_1));
  And_16_1 and_16_1_22 (.out_3(out_14), .in_2(in_2[9]), .in_1(in_1));
  And_16_1 and_16_1_23 (.out_3(out_30), .in_2(in_2[8]), .in_1(in_1));
  And_16_1 and_16_1_24 (.out_3(out_29), .in_2(in_2[10]), .in_1(in_1));
  And_16_1 and_16_1_25 (.out_3(out_15), .in_2(in_2[7]), .in_1(in_1));
  And_16_1 and_16_1_26 (.out_3(out_16), .in_2(in_2[5]), .in_1(in_1));
  And_16_1 and_16_1_27 (.out_3(out_31), .in_2(in_2[6]), .in_1(in_1));
  And_16_1 and_16_1_28 (.out_3(out_17), .in_2(in_2[3]), .in_1(in_1));
  And_16_1 and_16_1_29 (.out_3(out_32), .in_2(in_2[4]), .in_1(in_1));
  And_16_1 and_16_1_30 (.out_3(out_18), .in_2(in_2[1]), .in_1(in_1));
  And_16_1 and_16_1_31 (.out_3(out_34), .in_2(in_2[0]), .in_1(in_1));
  And_16_1 and_16_1_32 (.out_3(out_33), .in_2(in_2[2]), .in_1(in_1));
endmodule

module And_16_1 (
  input  [15:0] in_1,
  input  in_2,
  output [15:0] out_3
);

  wire [15:0] bit_extender_1_out;

  assign bit_extender_1_out = {{15{in_2}}, in_2};  // Bit_Extender bit_extender_1
  assign out_3 = bit_extender_1_out & in_1;  // AND_Gate and_1, 16 bits wide
endmodule

module Shift_32_Back_Forth (
  input  in_1,
  input  [4:0] in_2,
  input  in_3,
  input  in_4,
  input  [31:0] in_5,
  input  [31:0] in_6,
  output [31:0] out_7
);

  wire comparator_1_eq, comparator_2_eq, j_k_ff_1_q, or_1_out;
  wire [31:0] and_1_out, and_2_out, and_3_out, bit_extender_1_out, bit_extender_2_out, bit_extender_3_out,
       divider_1_out, multiplier_1_out, or_2_out, register_1_q, shifter_1_out;

  assign bit_extender_1_out = {{31{in_1}}, in_1};  // Bit_Extender bit_extender_1
  assign bit_extender_2_out = {{31{1'b0}}, in_1};  // Bit_Extender bit_extender_2
  Shifter #(.width(32)) shifter_1 (.in(bit_extender_2_out), .\dist (in_2), .out(shifter_1_out));
  or or_1 (or_1_out, in_3, in_4);
  assign bit_extender_3_out = {{31{j_k_ff_1_q}}, j_k_ff_1_q};  // Bit_Extender bit_extender_3
  J_K_Flip_Flop j_k_ff_1 (
    .J(comparator_1_eq), .clk(in_4), .K(comparator_2_eq), .Q(j_k_ff_1_q), .en(1'b1));  // open: Qn, preset, reset
  assign and_1_out = ~bit_extender_1_out & out_7;  // AND_Gate and_1, 32 bits wide
  assign or_2_out = shifter_1_out | and_1_out;  // OR_Gate or_2, 32 bits wide
  Register #(.width(32)) register_1 (.D(or_2_out), .en(1'b1), .Q(register_1_q), .clk(or_1_out));  // open: clr
  Multiplier #(.width(32)) multiplier_1 (.a(register_1_q), .b(32'h2), .out(multiplier_1_out));  // open: cin, cout
  Divider #(.width(32)) divider_1 (.a(register_1_q), .b(32'h2), .out(divider_1_out));  // open: upper, rem
  Comparator #(.width(32), .mode("unsigned")) comparator_1 (.a(in_5), .b(out_7), .eq(comparator_1_eq));  // open: gt, lt
  Comparator #(.width(32), .mode("unsigned")) comparator_2 (.a(in_6), .b(out_7), .eq(comparator_2_eq));  // open: gt, lt
  assign and_2_out = multiplier_1_out & ~bit_extender_3_out;  // AND_Gate and_2, 32 bits wide
  assign out_7 = and_2_out | and_3_out;  // OR_Gate or_3, 32 bits wide
  assign and_3_out = divider_1_out & bit_extender_3_out;  // AND_Gate and_3, 32 bits wide
endmodule

module paddle_controler (
  input  in_1,
  input  in_2,
  input  in_3,
  input  [6:0] in_4,
  input  [6:0] in_5,
  input  [6:0] in_6,
  output [15:0] out_7
);

  wire and_1_out, and_2_out, and_3_out, and_4_out, comparator_1_eq, comparator_2_eq, comparator_3_lt,
       comparator_4_gt, j_k_ff_1_qn, or_1_out, or_2_out, or_3_out;
  wire [2:0] bit_extender_1_out;
  wire [15:0] and_5_out, and_6_out, and_7_out, bit_extender_2_out, bit_extender_3_out, bit_extender_4_out,
       divider_1_out, multiplier_1_out, or_4_out, register_1_q, shifter_1_out;

  Comparator #(.width(7), .mode("unsigned")) comparator_1 (.a(in_4), .b(in_5), .eq(comparator_1_eq));  // open: gt, lt
  Comparator #(.width(7), .mode("unsigned")) comparator_2 (.a(in_6), .b(in_4), .eq(comparator_2_eq));  // open: gt, lt
  and and_1 (and_1_out, in_3, or_1_out);
  or or_1 (or_1_out, comparator_1_eq, comparator_2_eq);
  and and_2 (and_2_out, comparator_3_lt, comparator_1_eq);
  and and_3 (and_3_out, comparator_4_gt, comparator_2_eq);
  or or_2 (or_2_out, and_2_out, and_3_out);
  assign bit_extender_1_out = {{2{in_1}}, in_1};  // Bit_Extender bit_extender_1
  and and_4 (and_4_out, and_1_out, or_2_out);
  assign bit_extender_2_out = {{15{in_1}}, in_1};  // Bit_Extender bit_extender_2
  assign bit_extender_3_out = {{13{1'b0}}, bit_extender_1_out};  // Bit_Extender bit_extender_3
  Shifter #(.width(16)) shifter_1 (.in(bit_extender_3_out), .\dist (4'b0100), .out(shifter_1_out));
  or or_3 (or_3_out, in_2, and_4_out);
  J_K_Flip_Flop j_k_ff_1 (
    .J(comparator_1_eq), .clk(and_4_out), .K(comparator_2_eq), .Qn(j_k_ff_1_qn), .en(1'b1));  // open: Q, preset, reset
  assign bit_extender_4_out = {{15{j_k_ff_1_qn}}, j_k_ff_1_qn};  // Bit_Extender bit_extender_4
  assign and_5_out = ~bit_extender_2_out & out_7;  // AND_Gate and_5, 16 bits wide
  assign or_4_out = shifter_1_out | and_5_out;  // OR_Gate or_4, 16 bits wide
  Register #(.width(16)) register_1 (.D(or_4_out), .en(1'b1), .Q(register_1_q), .clk(or_3_out));  // open: clr
  Multiplier #(.width(16)) multiplier_1 (.a(register_1_q), .b(16'h2), .out(multiplier_1_out));  // open: cin, cout
  Divider #(.width(16)) divider_1 (.a(register_1_q), .b(16'h2), .out(divider_1_out));  // open: upper, rem
  assign and_6_out = multiplier_1_out & ~bit_extender_4_out;  // AND_Gate and_6, 16 bits wide
  assign out_7 = and_6_out | and_7_out;  // OR_Gate or_5, 16 bits wide
  assign and_7_out = divider_1_out & bit_extender_4_out;  // AND_Gate and_7, 16 bits wide
  Comparator #(.width(16), .mode("unsigned")) comparator_3 (
    .a(out_7), .b(16'he000), .lt(comparator_3_lt));  // open: gt, eq
  Comparator #(.width(16), .mode("unsigned")) comparator_4 (
    .a(out_7), .b(16'h7), .gt(comparator_4_gt));  // open: eq, lt
endmodule

module Reset_Clock_controler (
  input  in_1,
  input  in_2,
  output out_3,
  output out_4,
  output out_5,
  output out_6
);

  wire and_1_out, and_2_out, or_2_out, shift_register_1_q0, shift_register_1_q2, t_ff_1_q;

  and and_1 (and_1_out, in_2, and_2_out);
  and and_2 (and_2_out, ~shift_register_1_q2, ~out_6, ~shift_register_1_q0);  // AND_Gate
  Shift_Register #(.length(3)) shift_register_1 (
    .shift(1'b1), .in(and_1_out), .clk(in_1), .q0(shift_register_1_q0), .q1(out_6), .q2(shift_register_1_q2));  // open: out, load, clr, d0, d1, d2
  or or_1 (out_5, shift_register_1_q0, out_6);
  or or_2 (or_2_out, shift_register_1_q2, out_6, shift_register_1_q0);
  and and_3 (out_3, in_1, ~or_2_out);  // AND_Gate
  T_Flip_Flop t_ff_1 (.clk(out_3), .T(1'b1), .Q(t_ff_1_q), .en(1'b1));  // open: Qn, preset, reset
  T_Flip_Flop t_ff_2 (.clk(t_ff_1_q), .T(1'b1), .Q(out_4), .en(1'b1));  // open: Qn, preset, reset
endmodule
