// Logisim project Screen Controller.circ as structural Verilog: 3 circuits, main circuit main
module main (
  input  in_1
);

  wire and_1_out, and_2_out, clock_1_out, clock_2_out, clock_3_out, comparator_1_eq, not_3_out, not_4_out,
       t_ff_1_q;
  wire [4:0] bit_extender_2_out;
  wire [7:0] counter_1_q, ram_1_data, transmission_3_p1;
  wire [23:0] bit_extender_1_out, transmission_1_p1, transmission_1_p2;
  wire [31:0] counter_2_q, divider_1_out, screen_controller_1_out_4, screen_controller_1_out_5,
       screen_controller_1_out_6, screen_controller_1_out_7, screen_controller_1_out_8,
       screen_controller_1_out_9, screen_controller_1_out_10, screen_controller_1_out_11,
       screen_controller_1_out_12, screen_controller_1_out_13, screen_controller_1_out_14,
       screen_controller_1_out_15, screen_controller_1_out_16, screen_controller_1_out_17,
       screen_controller_1_out_18, screen_controller_1_out_19, screen_controller_1_out_20,
       screen_controller_1_out_21, screen_controller_1_out_22, screen_controller_1_out_23,
       screen_controller_1_out_24, screen_controller_1_out_25, screen_controller_1_out_26,
       screen_controller_1_out_27, screen_controller_1_out_28, screen_controller_1_out_29,
       screen_controller_1_out_30, screen_controller_1_out_31, screen_controller_1_out_32,
       screen_controller_1_out_33, screen_controller_1_out_34, screen_controller_1_out_35, shifter_1_out;

  Clock clock_1 (.out(clock_1_out));
  Clock clock_2 (.out(clock_2_out));
  Comparator #(.mode("unsigned")) comparator_1 (.a(counter_1_q), .b({8{1'b0}}), .eq(comparator_1_eq));  // open: gt, lt
  T_Flip_Flop t_ff_1 (.clk(comparator_1_eq), .T(1'b1), .Q(t_ff_1_q), .en(1'b1));  // open: Qn, preset, reset
  Counter #(.max('h80)) counter_1 (.count(1'b1), .Q(counter_1_q), .clk(clock_1_out));  // open: load, D, carry, clr
  and and_1 (and_1_out, clock_2_out, t_ff_1_q);
  // NOT_Gate not_1 has open pins: in=t_ff_1_q, out=open
  // NOT_Gate not_2 has open pins: in=not_3_out, out=open
  not not_3 (not_3_out, t_ff_1_q);
  assign bit_extender_1_out = {{16{1'b0}}, counter_1_q};  // Bit_Extender bit_extender_1
  DotMatrix #(.matrixcols(32), .matrixrows(32)) dotmatrix_1 (
    .col0(screen_controller_1_out_4), .col1(screen_controller_1_out_20), .col2(screen_controller_1_out_5),
    .col3(screen_controller_1_out_21), .col4(screen_controller_1_out_6), .col5(screen_controller_1_out_22),
    .col6(screen_controller_1_out_7), .col7(screen_controller_1_out_23), .col8(screen_controller_1_out_8),
    .col9(screen_controller_1_out_24), .col10(screen_controller_1_out_9), .col11(screen_controller_1_out_25),
    .col12(screen_controller_1_out_10), .col13(screen_controller_1_out_26),
    .col14(screen_controller_1_out_11), .col15(screen_controller_1_out_27),
    .col16(screen_controller_1_out_12), .col17(screen_controller_1_out_28),
    .col18(screen_controller_1_out_13), .col19(screen_controller_1_out_29),
    .col20(screen_controller_1_out_14), .col21(screen_controller_1_out_30),
    .col22(screen_controller_1_out_15), .col23(screen_controller_1_out_31),
    .col24(screen_controller_1_out_16), .col25(screen_controller_1_out_32),
    .col26(screen_controller_1_out_17), .col27(screen_controller_1_out_33),
    .col28(screen_controller_1_out_18), .col29(screen_controller_1_out_34),
    .col30(screen_controller_1_out_19), .col31(screen_controller_1_out_35));
  // Transmission_Gate #(.width(24)) transmission_1: pin names not known; wires that end beside it: transmission_1_p1, transmission_1_p2, t_ff_1_q
  // Transmission_Gate #(.width(24)) transmission_2: pin names not known; wires that end beside it: counter_1_q, bit_extender_1_out, not_3_out
  Clock clock_3 (.out(clock_3_out));
  not not_4 (not_4_out, not_3_out);
  and and_2 (and_2_out, not_3_out, clock_3_out);
  Counter #(.width(32), .max('hffffffff)) counter_2 (
    .count(1'b1), .Q(counter_2_q), .clk(clock_3_out));  // open: load, D, carry, clr
  Divider #(.width(32)) divider_1 (.a(counter_2_q), .b(32'h1f80), .out(divider_1_out));  // open: upper, rem
  RAM #(.addrWidth(24)) ram_1 (
    .addr(transmission_1_p2), .data(ram_1_data), .sel(1'b1), .clk(and_2_out), .ld(not_4_out), .clr(in_1));
  // NOT_Gate not_5 has open pins: in=not_3_out, out=open
  Shifter #(.width(32), .shift("lr")) shifter_1 (.in(counter_2_q), .\dist (bit_extender_2_out), .out(shifter_1_out));
  Bit_Extender #(.in_width(32), .out_width(5)) bit_extender_2 (.in(divider_1_out), .out(bit_extender_2_out));
  // Probe on bit_extender_2_out
  // Transmission_Gate #(.width(8)) transmission_3: pin names not known; wires that end beside it: transmission_3_p1, not_3_out
  // Probe on ram_1_data
  Bit_Extender #(.in_width(32), .out_width(8)) bit_extender_3 (.in(shifter_1_out), .out(transmission_3_p1));
  Screen_Controller screen_controller_1 (
    .in_1(and_1_out), .in_2(ram_1_data), .in_3({24{1'b0}}), .out_4(screen_controller_1_out_4),
    .out_20(screen_controller_1_out_20), .out_5(screen_controller_1_out_5),
    .out_21(screen_controller_1_out_21), .out_6(screen_controller_1_out_6),
    .out_22(screen_controller_1_out_22), .out_7(screen_controller_1_out_7),
    .out_23(screen_controller_1_out_23), .out_8(screen_controller_1_out_8),
    .out_24(screen_controller_1_out_24), .out_9(screen_controller_1_out_9),
    .out_25(screen_controller_1_out_25), .out_10(screen_controller_1_out_10),
    .out_26(screen_controller_1_out_26), .out_11(screen_controller_1_out_11),
    .out_27(screen_controller_1_out_27), .out_12(screen_controller_1_out_12),
    .out_28(screen_controller_1_out_28), .out_13(screen_controller_1_out_13),
    .out_29(screen_controller_1_out_29), .out_14(screen_controller_1_out_14),
    .out_30(screen_controller_1_out_30), .out_15(screen_controller_1_out_15),
    .out_31(screen_controller_1_out_31), .out_16(screen_controller_1_out_16),
    .out_32(screen_controller_1_out_32), .out_17(screen_controller_1_out_17),
    .out_33(screen_controller_1_out_33), .out_18(screen_controller_1_out_18),
    .out_34(screen_controller_1_out_34), .out_19(screen_controller_1_out_19),
    .out_35(screen_controller_1_out_35), .out_36(transmission_1_p1));
endmodule

module Screen_Controller (
  input  in_1,
  input  [7:0] in_2,
  input  [23:0] in_3,
  output [31:0] out_4,
  output [31:0] out_5,
  output [31:0] out_6,
  output [31:0] out_7,
  output [31:0] out_8,
  output [31:0] out_9,
  output [31:0] out_10,
  output [31:0] out_11,
  output [31:0] out_12,
  output [31:0] out_13,
  output [31:0] out_14,
  output [31:0] out_15,
  output [31:0] out_16,
  output [31:0] out_17,
  output [31:0] out_18,
  output [31:0] out_19,
  output [31:0] out_20,
  output [31:0] out_21,
  output [31:0] out_22,
  output [31:0] out_23,
  output [31:0] out_24,
  output [31:0] out_25,
  output [31:0] out_26,
  output [31:0] out_27,
  output [31:0] out_28,
  output [31:0] out_29,
  output [31:0] out_30,
  output [31:0] out_31,
  output [31:0] out_32,
  output [31:0] out_33,
  output [31:0] out_34,
  output [31:0] out_35,
  output [23:0] out_36
);

  wire demultiplexer_1_out0, demultiplexer_1_out1, demultiplexer_1_out2, demultiplexer_1_out3,
       demultiplexer_2_out0, demultiplexer_2_out1, demultiplexer_2_out2, demultiplexer_2_out3,
       demultiplexer_2_out4, demultiplexer_2_out5, demultiplexer_2_out6, demultiplexer_2_out7,
       demultiplexer_2_out8, demultiplexer_2_out9, demultiplexer_2_out10, demultiplexer_2_out11,
       demultiplexer_2_out12, demultiplexer_2_out13, demultiplexer_2_out14, demultiplexer_2_out15,
       demultiplexer_2_out16, demultiplexer_2_out17, demultiplexer_2_out18, demultiplexer_2_out19,
       demultiplexer_2_out20, demultiplexer_2_out21, demultiplexer_2_out22, demultiplexer_2_out23,
       demultiplexer_2_out24, demultiplexer_2_out25, demultiplexer_2_out26, demultiplexer_2_out27,
       demultiplexer_2_out28, demultiplexer_2_out29, demultiplexer_2_out30, demultiplexer_2_out31,
       screen_mem_access_1_out_6, screen_mem_access_1_out_8, screen_mem_access_2_out_6,
       screen_mem_access_2_out_8, screen_mem_access_3_out_6, screen_mem_access_3_out_8,
       screen_mem_access_4_out_6, screen_mem_access_4_out_8, screen_mem_access_5_out_6,
       screen_mem_access_5_out_8, screen_mem_access_6_out_6, screen_mem_access_6_out_8,
       screen_mem_access_7_out_6, screen_mem_access_7_out_8, screen_mem_access_8_out_6,
       screen_mem_access_8_out_8, screen_mem_access_9_out_6, screen_mem_access_9_out_8,
       screen_mem_access_10_out_6, screen_mem_access_10_out_8, screen_mem_access_11_out_6,
       screen_mem_access_11_out_8, screen_mem_access_12_out_6, screen_mem_access_12_out_8,
       screen_mem_access_13_out_6, screen_mem_access_13_out_8, screen_mem_access_14_out_6,
       screen_mem_access_14_out_8, screen_mem_access_15_out_6, screen_mem_access_15_out_8,
       screen_mem_access_16_out_6, screen_mem_access_16_out_8, screen_mem_access_17_out_6,
       screen_mem_access_17_out_8, screen_mem_access_18_out_6, screen_mem_access_18_out_8,
       screen_mem_access_19_out_6, screen_mem_access_19_out_8, screen_mem_access_20_out_6,
       screen_mem_access_20_out_8, screen_mem_access_21_out_6, screen_mem_access_21_out_8,
       screen_mem_access_22_out_6, screen_mem_access_22_out_8, screen_mem_access_23_out_6,
       screen_mem_access_23_out_8, screen_mem_access_24_out_6, screen_mem_access_24_out_8,
       screen_mem_access_25_out_6, screen_mem_access_25_out_8, screen_mem_access_26_out_6,
       screen_mem_access_26_out_8, screen_mem_access_27_out_6, screen_mem_access_27_out_8,
       screen_mem_access_28_out_6, screen_mem_access_28_out_8, screen_mem_access_29_out_6,
       screen_mem_access_29_out_8, screen_mem_access_30_out_6, screen_mem_access_30_out_8,
       screen_mem_access_31_out_6, screen_mem_access_32_out_6;
  wire [1:0] bit_extender_3_out;
  wire [4:0] and_1_out, and_2_out, and_3_out, and_4_out, bit_extender_1_out, bit_extender_4_out,
       bit_extender_5_out, bit_extender_6_out, bit_extender_7_out, or_2_out;
  wire [7:0] counter_1_q, divider_1_out, divider_1_rem;
  wire [23:0] bit_extender_2_out;
  wire [31:0] and_5_out, and_6_out, bit_extender_8_out, or_1_out, or_3_out, screen_mem_access_1_out_7,
       screen_mem_access_1_out_9, screen_mem_access_1_out_10, screen_mem_access_2_out_7,
       screen_mem_access_2_out_9, screen_mem_access_2_out_10, screen_mem_access_3_out_7,
       screen_mem_access_3_out_9, screen_mem_access_3_out_10, screen_mem_access_4_out_7,
       screen_mem_access_4_out_9, screen_mem_access_4_out_10, screen_mem_access_5_out_7,
       screen_mem_access_5_out_9, screen_mem_access_5_out_10, screen_mem_access_6_out_7,
       screen_mem_access_6_out_9, screen_mem_access_6_out_10, screen_mem_access_7_out_7,
       screen_mem_access_7_out_9, screen_mem_access_7_out_10, screen_mem_access_8_out_7,
       screen_mem_access_8_out_9, screen_mem_access_8_out_10, screen_mem_access_9_out_7,
       screen_mem_access_9_out_9, screen_mem_access_9_out_10, screen_mem_access_10_out_7,
       screen_mem_access_10_out_9, screen_mem_access_10_out_10, screen_mem_access_11_out_7,
       screen_mem_access_11_out_9, screen_mem_access_11_out_10, screen_mem_access_12_out_7,
       screen_mem_access_12_out_9, screen_mem_access_12_out_10, screen_mem_access_13_out_7,
       screen_mem_access_13_out_9, screen_mem_access_13_out_10, screen_mem_access_14_out_7,
       screen_mem_access_14_out_9, screen_mem_access_14_out_10, screen_mem_access_15_out_7,
       screen_mem_access_15_out_9, screen_mem_access_15_out_10, screen_mem_access_16_out_7,
       screen_mem_access_16_out_9, screen_mem_access_16_out_10, screen_mem_access_17_out_7,
       screen_mem_access_17_out_9, screen_mem_access_17_out_10, screen_mem_access_18_out_7,
       screen_mem_access_18_out_9, screen_mem_access_18_out_10, screen_mem_access_19_out_7,
       screen_mem_access_19_out_9, screen_mem_access_19_out_10, screen_mem_access_20_out_7,
       screen_mem_access_20_out_9, screen_mem_access_20_out_10, screen_mem_access_21_out_7,
       screen_mem_access_21_out_9, screen_mem_access_21_out_10, screen_mem_access_22_out_7,
       screen_mem_access_22_out_9, screen_mem_access_22_out_10, screen_mem_access_23_out_7,
       screen_mem_access_23_out_9, screen_mem_access_23_out_10, screen_mem_access_24_out_7,
       screen_mem_access_24_out_9, screen_mem_access_24_out_10, screen_mem_access_25_out_7,
       screen_mem_access_25_out_9, screen_mem_access_25_out_10, screen_mem_access_26_out_7,
       screen_mem_access_26_out_9, screen_mem_access_26_out_10, screen_mem_access_27_out_7,
       screen_mem_access_27_out_9, screen_mem_access_27_out_10, screen_mem_access_28_out_7,
       screen_mem_access_28_out_9, screen_mem_access_28_out_10, screen_mem_access_29_out_7,
       screen_mem_access_29_out_9, screen_mem_access_29_out_10, screen_mem_access_30_out_7,
       screen_mem_access_30_out_9, screen_mem_access_30_out_10, screen_mem_access_31_out_7,
       screen_mem_access_31_out_10, screen_mem_access_32_out_7, screen_mem_access_32_out_10, shifter_1_out,
       shifter_2_out;

  assign or_1_out = screen_mem_access_1_out_10 | screen_mem_access_2_out_10;  // OR_Gate or_1, 32 bits wide
  Divider divider_1 (.a(counter_1_q), .b(8'h4), .out(divider_1_out), .rem(divider_1_rem));  // open: upper
  Counter #(.max('h80)) counter_1 (.count(1'b1), .Q(counter_1_q), .clk(in_1));  // open: load, D, carry, clr
  Register #(.width(32)) register_1 (
    .D(screen_mem_access_1_out_7), .en(demultiplexer_2_out0), .Q(out_4), .clk(screen_mem_access_1_out_6));  // open: clr
  Screen_mem_access screen_mem_access_1 (
    .out_7(screen_mem_access_1_out_7), .in_2(in_1), .in_3(or_3_out), .out_10(screen_mem_access_1_out_10),
    .in_1(out_4), .out_8(screen_mem_access_1_out_8), .out_9(screen_mem_access_1_out_9),
    .in_4(screen_mem_access_3_out_10), .out_6(screen_mem_access_1_out_6), .in_5(demultiplexer_2_out0));
  Register #(.width(32)) register_2 (
    .D(screen_mem_access_2_out_7), .en(demultiplexer_2_out1), .Q(out_20), .clk(screen_mem_access_2_out_6));  // open: clr
  Screen_mem_access screen_mem_access_2 (
    .out_7(screen_mem_access_2_out_7), .in_2(in_1), .in_3(or_3_out), .out_10(screen_mem_access_2_out_10),
    .in_1(out_20), .out_8(screen_mem_access_2_out_8), .out_9(screen_mem_access_2_out_9),
    .in_4(screen_mem_access_4_out_10), .out_6(screen_mem_access_2_out_6), .in_5(demultiplexer_2_out1));
  Bit_Extender #(.out_width(5)) bit_extender_1 (.in(divider_1_out), .out(bit_extender_1_out));
  assign bit_extender_2_out = {{16{1'b0}}, counter_1_q};  // Bit_Extender bit_extender_2
  Register #(.width(32)) register_3 (
    .D(screen_mem_access_3_out_7), .en(demultiplexer_2_out2), .Q(out_5), .clk(screen_mem_access_3_out_6));  // open: clr
  Screen_mem_access screen_mem_access_3 (
    .out_7(screen_mem_access_3_out_7), .in_2(screen_mem_access_1_out_8), .in_3(screen_mem_access_1_out_9),
    .out_10(screen_mem_access_3_out_10), .in_1(out_5), .out_8(screen_mem_access_3_out_8),
    .out_9(screen_mem_access_3_out_9), .in_4(screen_mem_access_5_out_10), .out_6(screen_mem_access_3_out_6),
    .in_5(demultiplexer_2_out2));
  Register #(.width(32)) register_4 (
    .D(screen_mem_access_4_out_7), .en(demultiplexer_2_out3), .Q(out_21), .clk(screen_mem_access_4_out_6));  // open: clr
  Screen_mem_access screen_mem_access_4 (
    .out_7(screen_mem_access_4_out_7), .in_2(screen_mem_access_2_out_8), .in_3(screen_mem_access_2_out_9),
    .out_10(screen_mem_access_4_out_10), .in_1(out_21), .out_8(screen_mem_access_4_out_8),
    .out_9(screen_mem_access_4_out_9), .in_4(screen_mem_access_6_out_10), .out_6(screen_mem_access_4_out_6),
    .in_5(demultiplexer_2_out3));
  Demultiplexer #(.select(2), .disabled(0), .enable("false")) demultiplexer_1 (
    .out0(demultiplexer_1_out0), .out1(demultiplexer_1_out1), .out2(demultiplexer_1_out2),
    .out3(demultiplexer_1_out3), .in(1'b1), .sel(bit_extender_3_out));
  Bit_Extender #(.out_width(2)) bit_extender_3 (.in(divider_1_rem), .out(bit_extender_3_out));
  Adder #(.width(24)) adder_1 (.a(bit_extender_2_out), .b(in_3), .out(out_36));  // open: cin, cout
  Register #(.width(32)) register_5 (
    .D(screen_mem_access_5_out_7), .en(demultiplexer_2_out4), .Q(out_6), .clk(screen_mem_access_5_out_6));  // open: clr
  Screen_mem_access screen_mem_access_5 (
    .out_7(screen_mem_access_5_out_7), .in_2(screen_mem_access_3_out_8), .in_3(screen_mem_access_3_out_9),
    .out_10(screen_mem_access_5_out_10), .in_1(out_6), .out_8(screen_mem_access_5_out_8),
    .out_9(screen_mem_access_5_out_9), .in_4(screen_mem_access_7_out_10), .out_6(screen_mem_access_5_out_6),
    .in_5(demultiplexer_2_out4));
  Register #(.width(32)) register_6 (
    .D(screen_mem_access_6_out_7), .en(demultiplexer_2_out5), .Q(out_22), .clk(screen_mem_access_6_out_6));  // open: clr
  Screen_mem_access screen_mem_access_6 (
    .out_7(screen_mem_access_6_out_7), .in_2(screen_mem_access_4_out_8), .in_3(screen_mem_access_4_out_9),
    .out_10(screen_mem_access_6_out_10), .in_1(out_22), .out_8(screen_mem_access_6_out_8),
    .out_9(screen_mem_access_6_out_9), .in_4(screen_mem_access_8_out_10), .out_6(screen_mem_access_6_out_6),
    .in_5(demultiplexer_2_out5));
  Demultiplexer #(.select(5), .disabled(0), .enable("false")) demultiplexer_2 (
    .out0(demultiplexer_2_out0), .out1(demultiplexer_2_out1), .out2(demultiplexer_2_out2),
    .out3(demultiplexer_2_out3), .out4(demultiplexer_2_out4), .out5(demultiplexer_2_out5),
    .out6(demultiplexer_2_out6), .out7(demultiplexer_2_out7), .out8(demultiplexer_2_out8),
    .out9(demultiplexer_2_out9), .out10(demultiplexer_2_out10), .out11(demultiplexer_2_out11),
    .out12(demultiplexer_2_out12), .out13(demultiplexer_2_out13), .out14(demultiplexer_2_out14),
    .out15(demultiplexer_2_out15), .out16(demultiplexer_2_out16), .out17(demultiplexer_2_out17),
    .out18(demultiplexer_2_out18), .out19(demultiplexer_2_out19), .out20(demultiplexer_2_out20),
    .out21(demultiplexer_2_out21), .out22(demultiplexer_2_out22), .out23(demultiplexer_2_out23),
    .out24(demultiplexer_2_out24), .out25(demultiplexer_2_out25), .out26(demultiplexer_2_out26),
    .out27(demultiplexer_2_out27), .out28(demultiplexer_2_out28), .out29(demultiplexer_2_out29),
    .out30(demultiplexer_2_out30), .out31(demultiplexer_2_out31), .in(1'b1), .sel(bit_extender_1_out));
  Register #(.width(32)) register_7 (
    .D(screen_mem_access_7_out_7), .en(demultiplexer_2_out6), .Q(out_7), .clk(screen_mem_access_7_out_6));  // open: clr
  Screen_mem_access screen_mem_access_7 (
    .out_7(screen_mem_access_7_out_7), .in_2(screen_mem_access_5_out_8), .in_3(screen_mem_access_5_out_9),
    .out_10(screen_mem_access_7_out_10), .in_1(out_7), .out_8(screen_mem_access_7_out_8),
    .out_9(screen_mem_access_7_out_9), .in_4(screen_mem_access_9_out_10), .out_6(screen_mem_access_7_out_6),
    .in_5(demultiplexer_2_out6));
  Register #(.width(32)) register_8 (
    .D(screen_mem_access_8_out_7), .en(demultiplexer_2_out7), .Q(out_23), .clk(screen_mem_access_8_out_6));  // open: clr
  Screen_mem_access screen_mem_access_8 (
    .out_7(screen_mem_access_8_out_7), .in_2(screen_mem_access_6_out_8), .in_3(screen_mem_access_6_out_9),
    .out_10(screen_mem_access_8_out_10), .in_1(out_23), .out_8(screen_mem_access_8_out_8),
    .out_9(screen_mem_access_8_out_9), .in_4(screen_mem_access_10_out_10), .out_6(screen_mem_access_8_out_6),
    .in_5(demultiplexer_2_out7));
  assign bit_extender_4_out = {{4{demultiplexer_1_out0}}, demultiplexer_1_out0};  // Bit_Extender bit_extender_4
  assign bit_extender_5_out = {{4{demultiplexer_1_out1}}, demultiplexer_1_out1};  // Bit_Extender bit_extender_5
  assign bit_extender_6_out = {{4{demultiplexer_1_out2}}, demultiplexer_1_out2};  // Bit_Extender bit_extender_6
  assign bit_extender_7_out = {{4{demultiplexer_1_out3}}, demultiplexer_1_out3};  // Bit_Extender bit_extender_7
  Register #(.width(32)) register_9 (
    .D(screen_mem_access_9_out_7), .en(demultiplexer_2_out8), .Q(out_8), .clk(screen_mem_access_9_out_6));  // open: clr
  Screen_mem_access screen_mem_access_9 (
    .out_7(screen_mem_access_9_out_7), .in_2(screen_mem_access_7_out_8), .in_3(screen_mem_access_7_out_9),
    .out_10(screen_mem_access_9_out_10), .in_1(out_8), .out_8(screen_mem_access_9_out_8),
    .out_9(screen_mem_access_9_out_9), .in_4(screen_mem_access_11_out_10), .out_6(screen_mem_access_9_out_6),
    .in_5(demultiplexer_2_out8));
  Register #(.width(32)) register_10 (
    .D(screen_mem_access_10_out_7), .en(demultiplexer_2_out9), .Q(out_24), .clk(screen_mem_access_10_out_6));  // open: clr
  Screen_mem_access screen_mem_access_10 (
    .out_7(screen_mem_access_10_out_7), .in_2(screen_mem_access_8_out_8), .in_3(screen_mem_access_8_out_9),
    .out_10(screen_mem_access_10_out_10), .in_1(out_24), .out_8(screen_mem_access_10_out_8),
    .out_9(screen_mem_access_10_out_9), .in_4(screen_mem_access_12_out_10),
    .out_6(screen_mem_access_10_out_6), .in_5(demultiplexer_2_out9));
  assign and_1_out = {5{1'b0}} & bit_extender_4_out;  // AND_Gate and_1, 5 bits wide
  assign and_2_out = 5'b01000 & bit_extender_5_out;  // AND_Gate and_2, 5 bits wide
  assign and_3_out = 5'b10000 & bit_extender_6_out;  // AND_Gate and_3, 5 bits wide
  assign and_4_out = 5'b11000 & bit_extender_7_out;  // AND_Gate and_4, 5 bits wide
  Register #(.width(32)) register_11 (
    .D(screen_mem_access_11_out_7), .en(demultiplexer_2_out10), .Q(out_9), .clk(screen_mem_access_11_out_6));  // open: clr
  Screen_mem_access screen_mem_access_11 (
    .out_7(screen_mem_access_11_out_7), .in_2(screen_mem_access_9_out_8), .in_3(screen_mem_access_9_out_9),
    .out_10(screen_mem_access_11_out_10), .in_1(out_9), .out_8(screen_mem_access_11_out_8),
    .out_9(screen_mem_access_11_out_9), .in_4(screen_mem_access_13_out_10),
    .out_6(screen_mem_access_11_out_6), .in_5(demultiplexer_2_out10));
  Register #(.width(32)) register_12 (
    .D(screen_mem_access_12_out_7), .en(demultiplexer_2_out11), .Q(out_25), .clk(screen_mem_access_12_out_6));  // open: clr
  Screen_mem_access screen_mem_access_12 (
    .out_7(screen_mem_access_12_out_7), .in_2(screen_mem_access_10_out_8), .in_3(screen_mem_access_10_out_9),
    .out_10(screen_mem_access_12_out_10), .in_1(out_25), .out_8(screen_mem_access_12_out_8),
    .out_9(screen_mem_access_12_out_9), .in_4(screen_mem_access_14_out_10),
    .out_6(screen_mem_access_12_out_6), .in_5(demultiplexer_2_out11));
  assign bit_extender_8_out = {{24{1'b0}}, in_2};  // Bit_Extender bit_extender_8
  assign or_2_out = and_1_out | and_2_out | and_3_out | and_4_out;  // OR_Gate or_2, 5 bits wide
  Register #(.width(32)) register_13 (
    .D(screen_mem_access_13_out_7), .en(demultiplexer_2_out12), .Q(out_10), .clk(screen_mem_access_13_out_6));  // open: clr
  Screen_mem_access screen_mem_access_13 (
    .out_7(screen_mem_access_13_out_7), .in_2(screen_mem_access_11_out_8), .in_3(screen_mem_access_11_out_9),
    .out_10(screen_mem_access_13_out_10), .in_1(out_10), .out_8(screen_mem_access_13_out_8),
    .out_9(screen_mem_access_13_out_9), .in_4(screen_mem_access_15_out_10),
    .out_6(screen_mem_access_13_out_6), .in_5(demultiplexer_2_out12));
  Register #(.width(32)) register_14 (
    .D(screen_mem_access_14_out_7), .en(demultiplexer_2_out13), .Q(out_26), .clk(screen_mem_access_14_out_6));  // open: clr
  Screen_mem_access screen_mem_access_14 (
    .out_7(screen_mem_access_14_out_7), .in_2(screen_mem_access_12_out_8), .in_3(screen_mem_access_12_out_9),
    .out_10(screen_mem_access_14_out_10), .in_1(out_26), .out_8(screen_mem_access_14_out_8),
    .out_9(screen_mem_access_14_out_9), .in_4(screen_mem_access_16_out_10),
    .out_6(screen_mem_access_14_out_6), .in_5(demultiplexer_2_out13));
  Shifter #(.width(32)) shifter_1 (.in(bit_extender_8_out), .\dist (or_2_out), .out(shifter_1_out));
  Register #(.width(32)) register_15 (
    .D(screen_mem_access_15_out_7), .en(demultiplexer_2_out14), .Q(out_11), .clk(screen_mem_access_15_out_6));  // open: clr
  Screen_mem_access screen_mem_access_15 (
    .out_7(screen_mem_access_15_out_7), .in_2(screen_mem_access_13_out_8), .in_3(screen_mem_access_13_out_9),
    .out_10(screen_mem_access_15_out_10), .in_1(out_11), .out_8(screen_mem_access_15_out_8),
    .out_9(screen_mem_access_15_out_9), .in_4(screen_mem_access_17_out_10),
    .out_6(screen_mem_access_15_out_6), .in_5(demultiplexer_2_out14));
  Register #(.width(32)) register_16 (
    .D(screen_mem_access_16_out_7), .en(demultiplexer_2_out15), .Q(out_27), .clk(screen_mem_access_16_out_6));  // open: clr
  Screen_mem_access screen_mem_access_16 (
    .out_7(screen_mem_access_16_out_7), .in_2(screen_mem_access_14_out_8), .in_3(screen_mem_access_14_out_9),
    .out_10(screen_mem_access_16_out_10), .in_1(out_27), .out_8(screen_mem_access_16_out_8),
    .out_9(screen_mem_access_16_out_9), .in_4(screen_mem_access_18_out_10),
    .out_6(screen_mem_access_16_out_6), .in_5(demultiplexer_2_out15));
  assign and_5_out = or_1_out & ~shifter_2_out;  // AND_Gate and_5, 32 bits wide
  assign or_3_out = and_5_out | and_6_out;  // OR_Gate or_3, 32 bits wide
  assign and_6_out = shifter_1_out & shifter_2_out;  // AND_Gate and_6, 32 bits wide
  Shifter #(.width(32)) shifter_2 (.in(32'hff), .\dist (or_2_out), .out(shifter_2_out));
  Register #(.width(32)) register_17 (
    .D(screen_mem_access_17_out_7), .en(demultiplexer_2_out16), .Q(out_12), .clk(screen_mem_access_17_out_6));  // open: clr
  Screen_mem_access screen_mem_access_17 (
    .out_7(screen_mem_access_17_out_7), .in_2(screen_mem_access_15_out_8), .in_3(screen_mem_access_15_out_9),
    .out_10(screen_mem_access_17_out_10), .in_1(out_12), .out_8(screen_mem_access_17_out_8),
    .out_9(screen_mem_access_17_out_9), .in_4(screen_mem_access_19_out_10),
    .out_6(screen_mem_access_17_out_6), .in_5(demultiplexer_2_out16));
  Register #(.width(32)) register_18 (
    .D(screen_mem_access_18_out_7), .en(demultiplexer_2_out17), .Q(out_28), .clk(screen_mem_access_18_out_6));  // open: clr
  Screen_mem_access screen_mem_access_18 (
    .out_7(screen_mem_access_18_out_7), .in_2(screen_mem_access_16_out_8), .in_3(screen_mem_access_16_out_9),
    .out_10(screen_mem_access_18_out_10), .in_1(out_28), .out_8(screen_mem_access_18_out_8),
    .out_9(screen_mem_access_18_out_9), .in_4(screen_mem_access_20_out_10),
    .out_6(screen_mem_access_18_out_6), .in_5(demultiplexer_2_out17));
  // Probe on or_3_out
  Register #(.width(32)) register_19 (
    .D(screen_mem_access_19_out_7), .en(demultiplexer_2_out18), .Q(out_13), .clk(screen_mem_access_19_out_6));  // open: clr
  Screen_mem_access screen_mem_access_19 (
    .out_7(screen_mem_access_19_out_7), .in_2(screen_mem_access_17_out_8), .in_3(screen_mem_access_17_out_9),
    .out_10(screen_mem_access_19_out_10), .in_1(out_13), .out_8(screen_mem_access_19_out_8),
    .out_9(screen_mem_access_19_out_9), .in_4(screen_mem_access_21_out_10),
    .out_6(screen_mem_access_19_out_6), .in_5(demultiplexer_2_out18));
  Register #(.width(32)) register_20 (
    .D(screen_mem_access_20_out_7), .en(demultiplexer_2_out19), .Q(out_29), .clk(screen_mem_access_20_out_6));  // open: clr
  Screen_mem_access screen_mem_access_20 (
    .out_7(screen_mem_access_20_out_7), .in_2(screen_mem_access_18_out_8), .in_3(screen_mem_access_18_out_9),
    .out_10(screen_mem_access_20_out_10), .in_1(out_29), .out_8(screen_mem_access_20_out_8),
    .out_9(screen_mem_access_20_out_9), .in_4(screen_mem_access_22_out_10),
    .out_6(screen_mem_access_20_out_6), .in_5(demultiplexer_2_out19));
  Register #(.width(32)) register_21 (
    .D(screen_mem_access_21_out_7), .en(demultiplexer_2_out20), .Q(out_14), .clk(screen_mem_access_21_out_6));  // open: clr
  Screen_mem_access screen_mem_access_21 (
    .out_7(screen_mem_access_21_out_7), .in_2(screen_mem_access_19_out_8), .in_3(screen_mem_access_19_out_9),
    .out_10(screen_mem_access_21_out_10), .in_1(out_14), .out_8(screen_mem_access_21_out_8),
    .out_9(screen_mem_access_21_out_9), .in_4(screen_mem_access_23_out_10),
    .out_6(screen_mem_access_21_out_6), .in_5(demultiplexer_2_out20));
  Register #(.width(32)) register_22 (
    .D(screen_mem_access_22_out_7), .en(demultiplexer_2_out21), .Q(out_30), .clk(screen_mem_access_22_out_6));  // open: clr
  Screen_mem_access screen_mem_access_22 (
    .out_7(screen_mem_access_22_out_7), .in_2(screen_mem_access_20_out_8), .in_3(screen_mem_access_20_out_9),
    .out_10(screen_mem_access_22_out_10), .in_1(out_30), .out_8(screen_mem_access_22_out_8),
    .out_9(screen_mem_access_22_out_9), .in_4(screen_mem_access_24_out_10),
    .out_6(screen_mem_access_22_out_6), .in_5(demultiplexer_2_out21));
  Register #(.width(32)) register_23 (
    .D(screen_mem_access_23_out_7), .en(demultiplexer_2_out22), .Q(out_15), .clk(screen_mem_access_23_out_6));  // open: clr
  Screen_mem_access screen_mem_access_23 (
    .out_7(screen_mem_access_23_out_7), .in_2(screen_mem_access_21_out_8), .in_3(screen_mem_access_21_out_9),
    .out_10(screen_mem_access_23_out_10), .in_1(out_15), .out_8(screen_mem_access_23_out_8),
    .out_9(screen_mem_access_23_out_9), .in_4(screen_mem_access_25_out_10),
    .out_6(screen_mem_access_23_out_6), .in_5(demultiplexer_2_out22));
  Register #(.width(32)) register_24 (
    .D(screen_mem_access_24_out_7), .en(demultiplexer_2_out23), .Q(out_31), .clk(screen_mem_access_24_out_6));  // open: clr
  Screen_mem_access screen_mem_access_24 (
    .out_7(screen_mem_access_24_out_7), .in_2(screen_mem_access_22_out_8), .in_3(screen_mem_access_22_out_9),
    .out_10(screen_mem_access_24_out_10), .in_1(out_31), .out_8(screen_mem_access_24_out_8),
    .out_9(screen_mem_access_24_out_9), .in_4(screen_mem_access_26_out_10),
    .out_6(screen_mem_access_24_out_6), .in_5(demultiplexer_2_out23));
  Register #(.width(32)) register_25 (
    .D(screen_mem_access_25_out_7), .en(demultiplexer_2_out24), .Q(out_16), .clk(screen_mem_access_25_out_6));  // open: clr
  Screen_mem_access screen_mem_access_25 (
    .out_7(screen_mem_access_25_out_7), .in_2(screen_mem_access_23_out_8), .in_3(screen_mem_access_23_out_9),
    .out_10(screen_mem_access_25_out_10), .in_1(out_16), .out_8(screen_mem_access_25_out_8),
    .out_9(screen_mem_access_25_out_9), .in_4(screen_mem_access_27_out_10),
    .out_6(screen_mem_access_25_out_6), .in_5(demultiplexer_2_out24));
  Register #(.width(32)) register_26 (
    .D(screen_mem_access_26_out_7), .en(demultiplexer_2_out25), .Q(out_32), .clk(screen_mem_access_26_out_6));  // open: clr
  Screen_mem_access screen_mem_access_26 (
    .out_7(screen_mem_access_26_out_7), .in_2(screen_mem_access_24_out_8), .in_3(screen_mem_access_24_out_9),
    .out_10(screen_mem_access_26_out_10), .in_1(out_32), .out_8(screen_mem_access_26_out_8),
    .out_9(screen_mem_access_26_out_9), .in_4(screen_mem_access_28_out_10),
    .out_6(screen_mem_access_26_out_6), .in_5(demultiplexer_2_out25));
  Register #(.width(32)) register_27 (
    .D(screen_mem_access_27_out_7), .en(demultiplexer_2_out26), .Q(out_17), .clk(screen_mem_access_27_out_6));  // open: clr
  Screen_mem_access screen_mem_access_27 (
    .out_7(screen_mem_access_27_out_7), .in_2(screen_mem_access_25_out_8), .in_3(screen_mem_access_25_out_9),
    .out_10(screen_mem_access_27_out_10), .in_1(out_17), .out_8(screen_mem_access_27_out_8),
    .out_9(screen_mem_access_27_out_9), .in_4(screen_mem_access_29_out_10),
    .out_6(screen_mem_access_27_out_6), .in_5(demultiplexer_2_out26));
  Register #(.width(32)) register_28 (
    .D(screen_mem_access_28_out_7), .en(demultiplexer_2_out27), .Q(out_33), .clk(screen_mem_access_28_out_6));  // open: clr
  Screen_mem_access screen_mem_access_28 (
    .out_7(screen_mem_access_28_out_7), .in_2(screen_mem_access_26_out_8), .in_3(screen_mem_access_26_out_9),
    .out_10(screen_mem_access_28_out_10), .in_1(out_33), .out_8(screen_mem_access_28_out_8),
    .out_9(screen_mem_access_28_out_9), .in_4(screen_mem_access_30_out_10),
    .out_6(screen_mem_access_28_out_6), .in_5(demultiplexer_2_out27));
  Register #(.width(32)) register_29 (
    .D(screen_mem_access_29_out_7), .en(demultiplexer_2_out28), .Q(out_18), .clk(screen_mem_access_29_out_6));  // open: clr
  Screen_mem_access screen_mem_access_29 (
    .out_7(screen_mem_access_29_out_7), .in_2(screen_mem_access_27_out_8), .in_3(screen_mem_access_27_out_9),
    .out_10(screen_mem_access_29_out_10), .in_1(out_18), .out_8(screen_mem_access_29_out_8),
    .out_9(screen_mem_access_29_out_9), .in_4(screen_mem_access_31_out_10),
    .out_6(screen_mem_access_29_out_6), .in_5(demultiplexer_2_out28));
  Register #(.width(32)) register_30 (
    .D(screen_mem_access_30_out_7), .en(demultiplexer_2_out29), .Q(out_34), .clk(screen_mem_access_30_out_6));  // open: clr
  Screen_mem_access screen_mem_access_30 (
    .out_7(screen_mem_access_30_out_7), .in_2(screen_mem_access_28_out_8), .in_3(screen_mem_access_28_out_9),
    .out_10(screen_mem_access_30_out_10), .in_1(out_34), .out_8(screen_mem_access_30_out_8),
    .out_9(screen_mem_access_30_out_9), .in_4(screen_mem_access_32_out_10),
    .out_6(screen_mem_access_30_out_6), .in_5(demultiplexer_2_out29));
  Register #(.width(32)) register_31 (
    .D(screen_mem_access_31_out_7), .en(demultiplexer_2_out30), .Q(out_19), .clk(screen_mem_access_31_out_6));  // open: clr
  Screen_mem_access screen_mem_access_31 (
    .out_7(screen_mem_access_31_out_7), .in_2(screen_mem_access_29_out_8), .in_3(screen_mem_access_29_out_9),
    .out_10(screen_mem_access_31_out_10), .in_1(out_19), .in_4({32{1'b0}}),
    .out_6(screen_mem_access_31_out_6), .in_5(demultiplexer_2_out30));  // open: out_8, out_9
  Register #(.width(32)) register_32 (
    .D(screen_mem_access_32_out_7), .en(demultiplexer_2_out31), .Q(out_35), .clk(screen_mem_access_32_out_6));  // open: clr
  Screen_mem_access screen_mem_access_32 (
    .out_7(screen_mem_access_32_out_7), .in_2(screen_mem_access_30_out_8), .in_3(screen_mem_access_30_out_9),
    .out_10(screen_mem_access_32_out_10), .in_1(out_35), .in_4({32{1'b0}}),
    .out_6(screen_mem_access_32_out_6), .in_5(demultiplexer_2_out31));  // open: out_8, out_9
endmodule

module Screen_mem_access (
  input  [31:0] in_1,
  input  in_2,
  input  [31:0] in_3,
  input  [31:0] in_4,
  input  in_5,
  output out_6,
  output [31:0] out_7,
  output out_8,
  output [31:0] out_9,
  output [31:0] out_10
);

  wire [31:0] and_2_out, and_3_out, bit_extender_1_out;

  assign out_10 = and_2_out | and_3_out;  // OR_Gate or_1, 32 bits wide
  assign out_7 = in_3 & bit_extender_1_out;  // AND_Gate and_1, 32 bits wide
  assign and_2_out = in_1 & bit_extender_1_out;  // AND_Gate and_2, 32 bits wide
  assign and_3_out = in_4 & ~bit_extender_1_out;  // AND_Gate and_3, 32 bits wide
  assign bit_extender_1_out = {{31{in_5}}, in_5};  // Bit_Extender bit_extender_1

  assign out_6 = in_2;
  assign out_8 = in_2;
  assign out_9 = in_3;
endmodule
