// Logisim project Signed Overflow Detect.circ as structural Verilog: 2 circuits, main circuit 1add
module main (
  input  A,
  input  in_2,
  input  in_3,
  input  in_4,
  input  in_5,
  input  in_6,
  input  in_7,
  input  in_8,
  input  B,
  input  in_10,
  input  in_11,
  input  in_12,
  input  in_13,
  input  in_14,
  input  in_15,
  input  in_16,
  input  _0_Add__1_Sub,
  output out_18,
  output out_19,
  output out_20,
  output out_21,
  output out_22,
  output out_23,
  output out_24,
  output out_25,
  output out_26,
  output Overflow
);

  wire n1add_1_out_5, n1add_1_out_6, n1add_3_out_5, n1add_3_out_6, n1add_4_out_5, n1add_4_out_6,
       n1add_5_out_5, n1add_5_out_6, n1add_6_out_5, n1add_6_out_6, n1add_7_out_5, n1add_7_out_6,
       n1add_8_out_5, n1add_8_out_6, xor_1_out, xor_2_out, xor_4_out;

  _1add u_1add_1 (
    .out_6(n1add_1_out_6), .in_4(n1add_3_out_6), .in_1(in_2), .in_2(in_10), .out_7(out_20),
    .in_3(n1add_3_out_5), .out_5(n1add_1_out_5));
  _1add u_1add_2 (
    .out_6(out_18), .in_4(n1add_1_out_6), .in_1(A), .in_2(B), .out_7(out_19), .in_3(n1add_1_out_5));  // open: out_5
  xor xor_1 (xor_1_out, out_19, out_18);
  xor xor_2 (xor_2_out, B, A);
  _1add u_1add_3 (
    .out_6(n1add_3_out_6), .in_4(n1add_4_out_6), .in_1(in_3), .in_2(in_11), .out_7(out_21),
    .in_3(n1add_4_out_5), .out_5(n1add_3_out_5));
  _1add u_1add_4 (
    .out_6(n1add_4_out_6), .in_4(n1add_5_out_6), .in_1(in_4), .in_2(in_12), .out_7(out_22),
    .in_3(n1add_5_out_5), .out_5(n1add_4_out_5));
  xor xor_3 (Overflow, _0_Add__1_Sub, xor_4_out);
  xor xor_4 (xor_4_out, xor_1_out, xor_2_out);
  _1add u_1add_5 (
    .out_6(n1add_5_out_6), .in_4(n1add_6_out_6), .in_1(in_5), .in_2(in_13), .out_7(out_23),
    .in_3(n1add_6_out_5), .out_5(n1add_5_out_5));
  _1add u_1add_6 (
    .out_6(n1add_6_out_6), .in_4(n1add_7_out_6), .in_1(in_6), .in_2(in_14), .out_7(out_24),
    .in_3(n1add_7_out_5), .out_5(n1add_6_out_5));
  _1add u_1add_7 (
    .out_6(n1add_7_out_6), .in_4(n1add_8_out_6), .in_1(in_7), .in_2(in_15), .out_7(out_25),
    .in_3(n1add_8_out_5), .out_5(n1add_7_out_5));
  _1add u_1add_8 (
    .out_6(n1add_8_out_6), .in_4(_0_Add__1_Sub), .in_1(in_8), .in_2(in_16), .out_7(out_26),
    .in_3(_0_Add__1_Sub), .out_5(n1add_8_out_5));
endmodule

module _1add (
  input  in_1,
  input  in_2,
  input  in_3,
  input  in_4,
  output out_5,
  output out_6,
  output out_7
);

  wire and_1_out, and_2_out, xor_1_out, xor_2_out;

  or or_1 (out_6, and_1_out, and_2_out);
  and and_1 (and_1_out, in_1, xor_1_out);
  and and_2 (and_2_out, xor_2_out, in_4);
  xor xor_1 (xor_1_out, in_2, in_3);
  xor xor_2 (xor_2_out, xor_1_out, in_1);
  xor xor_3 (out_7, xor_2_out, in_4);

  assign out_5 = in_3;
endmodule
