// Logisim project Simultaneous_Memeory_Access2.circ as structural Verilog: 11 circuits, main circuit main
module main (
  input  in_1,
  input  in_2,
  input  in_3,
  input  in_4,
  input  Reset,
  output [7:0] out_6
);

  wire arbitor_1_success, arbitor_1_success_2, arbitor_1_success_3, arbitor_1_success_4, clock_1_out,
       random_request_1_r_w_2, random_request_1_request, random_request_2_r_w_2, random_request_2_request,
       random_request_3_r_w_2, random_request_3_request, random_request_4_r_w_2, random_request_4_request;
  wire [7:0] random_request_1_out_6, random_request_1_out_8, random_request_2_out_6, random_request_2_out_8,
       random_request_3_out_6, random_request_3_out_8, random_request_4_out_6, random_request_4_out_8;

  Random_Request random_request_1 (
    .in_1(8'h2), .CLK(clock_1_out), .out_6(random_request_1_out_6), .Request(random_request_1_request),
    .out_8(random_request_1_out_8), .success(arbitor_1_success), .RST(Reset), .R_W_2(random_request_1_r_w_2),
    .R_W(in_1));
  Random_Request random_request_2 (
    .in_1(8'h4), .CLK(clock_1_out), .out_6(random_request_2_out_6), .Request(random_request_2_request),
    .out_8(random_request_2_out_8), .success(arbitor_1_success_2), .RST(Reset),
    .R_W_2(random_request_2_r_w_2), .R_W(in_2));
  Random_Request random_request_3 (
    .in_1(8'h6), .CLK(clock_1_out), .out_6(random_request_3_out_6), .Request(random_request_3_request),
    .out_8(random_request_3_out_8), .success(arbitor_1_success_3), .RST(Reset),
    .R_W_2(random_request_3_r_w_2), .R_W(in_3));
  Random_Request random_request_4 (
    .in_1(8'ha), .CLK(clock_1_out), .out_6(random_request_4_out_6), .Request(random_request_4_request),
    .out_8(random_request_4_out_8), .success(arbitor_1_success_4), .RST(Reset),
    .R_W_2(random_request_4_r_w_2), .R_W(in_4));
  Clock clock_1 (.out(clock_1_out));
  Arbitor arbitor_1 (
    .Address(random_request_1_out_6), .Request(random_request_1_request), .R_W(random_request_1_r_w_2),
    .Data(random_request_1_out_8), .Success(arbitor_1_success), .Address_2(random_request_2_out_6),
    .Request_2(random_request_2_request), .R_W_2(random_request_2_r_w_2), .Data_2(random_request_2_out_8),
    .Success_2(arbitor_1_success_2), .Address_3(random_request_3_out_6),
    .Request_3(random_request_3_request), .R_W_3(random_request_3_r_w_2), .Data_3(random_request_3_out_8),
    .Success_3(arbitor_1_success_3), .Address_4(random_request_4_out_6),
    .Request_4(random_request_4_request), .R_W_4(random_request_4_r_w_2), .Data_4(random_request_4_out_8),
    .Success_4(arbitor_1_success_4));
endmodule

module Arbitor (
  input  [7:0] Address,
  input  Request,
  input  R_W,
  input  [7:0] Data,
  input  [7:0] Address_2,
  input  Request_2,
  input  R_W_2,
  input  [7:0] Data_2,
  input  [7:0] Address_3,
  input  Request_3,
  input  R_W_3,
  input  [7:0] Data_3,
  input  [7:0] Address_4,
  input  Request_4,
  input  R_W_4,
  input  [7:0] Data_4,
  output Success,
  output Success_2,
  output Success_3,
  output Success_4
);

  Memory memory_1 ();  // open: Address, Data_In, Data_Out, CLK, R_W, RST, EN
endmodule

module Memory (
  input  [7:0] Address,
  input  R_W,
  input  RST,
  input  [7:0] Data_In,
  input  CLK,
  input  EN,
  output [7:0] Data_Out
);

  wire and_1_out, and_2_out, and_3_out, buffer_1_out, buffer_2_out, buffer_3_out, buffer_4_out, buffer_5_out,
       buffer_6_out, buffer_7_out, buffer_8_out, buffer_9_out, buffer_10_out, buffer_11_out, buffer_12_out,
       buffer_13_out, buffer_14_out, buffer_15_out, buffer_16_out, buffer_17_out, buffer_18_out,
       buffer_19_out, buffer_20_out, buffer_21_out, buffer_22_out, buffer_23_out, buffer_24_out,
       buffer_25_out, buffer_26_out, buffer_27_out, buffer_28_out, buffer_29_out, buffer_30_out,
       buffer_31_out, buffer_32_out, not_1_out, not_2_out, or_1_out;
  wire [7:0] ram_1_data;

  buf buffer_1 (buffer_1_out, buffer_9_out);
  buf buffer_2 (buffer_2_out, buffer_16_out);
  buf buffer_3 (buffer_3_out, buffer_22_out);
  buf buffer_4 (buffer_4_out, buffer_1_out);
  buf buffer_5 (buffer_5_out, buffer_6_out);
  buf buffer_6 (buffer_6_out, buffer_7_out);
  buf buffer_7 (buffer_7_out, buffer_4_out);
  buf buffer_8 (buffer_8_out, buffer_13_out);
  buf buffer_9 (buffer_9_out, buffer_10_out);
  buf buffer_10 (buffer_10_out, buffer_8_out);
  buf buffer_11 (buffer_11_out, buffer_14_out);
  buf buffer_12 (buffer_12_out, buffer_2_out);
  buf buffer_13 (buffer_13_out, buffer_11_out);
  buf buffer_14 (buffer_14_out, buffer_12_out);
  buf buffer_15 (buffer_15_out, buffer_17_out);
  buf buffer_16 (buffer_16_out, buffer_15_out);
  buf buffer_17 (buffer_17_out, buffer_19_out);
  buf buffer_18 (buffer_18_out, buffer_20_out);
  buf buffer_19 (buffer_19_out, buffer_21_out);
  buf buffer_20 (buffer_20_out, buffer_3_out);
  buf buffer_21 (buffer_21_out, buffer_18_out);
  buf buffer_22 (buffer_22_out, buffer_24_out);
  buf buffer_23 (buffer_23_out, CLK);
  buf buffer_24 (buffer_24_out, buffer_23_out);
  buf buffer_25 (buffer_25_out, CLK);
  buf buffer_26 (buffer_26_out, buffer_25_out);
  buf buffer_27 (buffer_27_out, not_1_out);
  buf buffer_28 (buffer_28_out, buffer_27_out);
  not not_1 (not_1_out, CLK);
  RAM ram_1 (.addr(Address), .data(ram_1_data), .sel(1'b1), .clk(buffer_5_out), .ld(not_2_out), .clr(RST));
  not not_2 (not_2_out, R_W);
  buf buffer_29 (buffer_29_out, buffer_26_out);
  buf buffer_30 (buffer_30_out, buffer_29_out);
  and and_1 (and_1_out, ~buffer_30_out, CLK);  // AND_Gate
  buf buffer_31 (buffer_31_out, buffer_28_out);
  buf buffer_32 (buffer_32_out, buffer_31_out);
  and and_2 (and_2_out, ~buffer_32_out, not_1_out);  // AND_Gate
  and and_3 (and_3_out, ~R_W, EN, CLK);  // AND_Gate
  Transistor #(.\type ("n"), .width(8)) transistor_1 (.in(Data_In), .out(ram_1_data), .gate(R_W));
  or or_1 (or_1_out, and_1_out, and_2_out);
  Multiplexer #(.width(8), .enable("false")) multiplexer_1 (
    .in0({8{1'b0}}), .in1(ram_1_data), .out(Data_Out), .sel(and_3_out));
endmodule

module Selector (
  input  in_1,
  input  in_2,
  input  in_3,
  input  in_4,
  output [1:0] out_5,
  output out_6
);

  wire and_1_out, and_2_out, and_3_out, or_1_out, or_2_out, or_3_out, priority_encoder_1_en_out;
  wire [1:0] priority_encoder_1_out;

  or or_1 (or_1_out, in_1, in_2);
  or or_2 (or_2_out, or_1_out, in_3);
  or or_3 (or_3_out, or_2_out, in_4);
  and and_1 (and_1_out, ~in_1, or_1_out);  // AND_Gate
  and and_2 (and_2_out, ~or_1_out, or_2_out);  // AND_Gate
  and and_3 (and_3_out, ~or_2_out, or_3_out);  // AND_Gate
  Priority_Encoder #(.select(2), .disabled(0)) priority_encoder_1 (
    .in0(in_1), .in1(and_1_out), .in2(and_2_out), .in3(and_3_out), .out(priority_encoder_1_out), .gs(out_6),
    .en_out(priority_encoder_1_en_out));  // open: en_in
  Multiplexer #(.width(2), .enable("false")) multiplexer_1 (
    .in0(priority_encoder_1_out), .in1(2'b00), .out(out_5), .sel(priority_encoder_1_en_out));
endmodule

module Random_Request (
  input  [7:0] in_1,
  input  CLK,
  input  R_W,
  input  success,
  input  RST,
  output [7:0] out_6,
  output Request,
  output [7:0] out_8,
  output R_W_2
);

  wire and_1_out, and_2_out, buffer_1_out, buffer_2_out, buffer_3_out, buffer_4_out, buffer_5_out,
       buffer_6_out, comparator_1_eq, comparator_1_lt, comparator_2_lt, or_1_out, or_2_out, or_3_out;
  wire [7:0] counter_1_q;

  Counter counter_1 (.load(1'b0), .count(1'b1), .Q(counter_1_q), .clk(CLK), .clr(or_1_out));  // open: D, carry
  or or_1 (or_1_out, comparator_1_lt, RST);
  Comparator #(.mode("unsigned")) comparator_1 (
    .a(in_1), .b(counter_1_q), .eq(comparator_1_eq), .lt(comparator_1_lt));  // open: gt
  and and_1 (and_1_out, comparator_1_eq, ~Request);  // AND_Gate
  buf buffer_1 (buffer_1_out, buffer_5_out);
  buf buffer_2 (buffer_2_out, and_1_out);
  buf buffer_3 (buffer_3_out, buffer_2_out);
  Counter counter_2 (.load(1'b0), .count(1'b1), .Q(out_6), .clk(and_1_out), .clr(or_2_out));  // open: D, carry
  or or_2 (or_2_out, comparator_2_lt, RST);
  and and_2 (and_2_out, RST, ~buffer_1_out);  // AND_Gate
  buf buffer_4 (buffer_4_out, buffer_6_out);
  buf buffer_5 (buffer_5_out, buffer_4_out);
  buf buffer_6 (buffer_6_out, RST);
  D_Flip_Flop d_ff_1 (.clk(buffer_3_out), .D(and_1_out), .Q(Request), .en(1'b1), .reset(or_3_out));  // open: Qn, preset
  or or_3 (or_3_out, success, RST);
  Comparator #(.mode("unsigned")) comparator_2 (.a(8'h20), .b(out_6), .lt(comparator_2_lt));  // open: gt, eq
  Random random_1 (.clk(and_1_out), .out(out_8), .clr(and_2_out));  // open: next

  assign R_W_2 = R_W;
endmodule

module MemBank (
  input  [5:0] in_1
);

  wire undriven, undriven_3;
  wire [7:0] and8_1_out_3, bit_extender_1_out, or82_1_out_3, register_1_q, undriven_2;

  assign bit_extender_1_out = {{7{1'b0}}, undriven};  // Bit_Extender bit_extender_1
  Register register_1 (.D(undriven_2), .en(undriven), .Q(register_1_q), .clk(undriven_3));  // open: clr
  And8 and8_1 (.in_1(bit_extender_1_out), .out_3(and8_1_out_3), .in_2(register_1_q));
  OR82 or82_1 (.in_2(and8_1_out_3), .out_3(or82_1_out_3), .in_1(register_1_q));
  Decoder #(.select(4), .disabled(0), .enable("false")) decoder_1 (.sel(in_1[5:2]));  // open: out0, out1, out2, out3, out4, out5, out6, out7, out8, out9, out10, out11, out12, out13, out14, out15
endmodule

module Or8 (
  input  [7:0] in_1,
  input  [7:0] in_2,
  output [7:0] out_3
);

  assign out_3 = in_1 | in_2;  // OR_Gate or_1, 8 bits wide
endmodule

module OR82 (
  input  [7:0] in_1,
  input  [7:0] in_2,
  output [7:0] out_3
);

  assign out_3 = in_1 | in_2;  // OR_Gate or_1, 8 bits wide
endmodule

module And8 (
  input  [7:0] in_1,
  input  [7:0] in_2,
  output [7:0] out_3
);

  assign out_3 = in_1 & in_2;  // AND_Gate and_1, 8 bits wide
endmodule

module And82 (
  input  [7:0] in_1,
  input  [7:0] in_2,
  output [7:0] out_3
);

  assign out_3 = in_1 & in_2;  // AND_Gate and_1, 8 bits wide
endmodule

module Sel1 (
  input  [7:0] in_1,
  output out_2
);

  BitSelector bitselector_1 (.in(in_1), .out(out_2), .sel(3'b000));
endmodule
